// Logisim project ULA.circ as structural Verilog: 18 circuits, main circuit main
module main (
  input  A7,
  input  A6,
  input  A5,
  input  A4,
  input  A3,
  input  A2,
  input  A1,
  input  A0,
  input  B7,
  input  B6,
  input  B5,
  input  B4,
  input  B3,
  input  B2,
  input  B1,
  input  B0,
  input  in_17,
  input  in_18,
  input  in_19,
  output R7,
  output R6,
  output R5,
  output R4,
  output R3,
  output R2,
  output R1,
  output R0,
  output out_28
);

  wire divOVERFLOW, multOVERFLOW, SINAL, SINALresto, somaOVERFLOW;
  wire [6:0] divR;
  wire [7:0] demultiplexer_1_out3, demultiplexer_1_out4, demultiplexer_2_out3, demultiplexer_2_out4, divA,
       divB, multA, multB, multR, Resto, somaA, somaB, somaR, subA, subB, subR;

  Resto resto_1 (
    .sinal(SINALresto), .A7(divA[7]), .A6(divA[6]), .A5(divA[5]), .A4(divA[4]), .A3(divA[3]), .A2(divA[2]),
    .A1(divA[1]), .A0(divA[0]), .B7(divB[7]), .B6(divB[6]), .B5(divB[5]), .B4(divB[4]), .B3(divB[3]),
    .B2(divB[2]), .B1(divB[1]), .B0(divB[0]), .Q7(divOVERFLOW), .Q6(divR[6]), .Q5(divR[5]), .Q4(divR[4]),
    .Q3(divR[3]), .Q2(divR[2]), .Q1(divR[1]), .Q0(divR[0]), .R7(Resto[7]), .R6(Resto[6]), .R5(Resto[5]),
    .R4(Resto[4]), .R3(Resto[3]), .R2(Resto[2]), .R1(Resto[1]), .R0(Resto[0]));
  Adder8Bit adder8bit_1 (
    .A0(somaA[0]), .A1(somaA[1]), .A2(somaA[2]), .A3(somaA[3]), .A4(somaA[4]), .A5(somaA[5]), .A6(somaA[6]),
    .A7(somaA[7]), .B0(somaB[0]), .B1(somaB[1]), .B2(somaB[2]), .B3(somaB[3]), .B4(somaB[4]), .B5(somaB[5]),
    .B6(somaB[6]), .B7(somaB[7]), .OVERFLOW(somaOVERFLOW), .R7(somaR[7]), .R6(somaR[6]), .R5(somaR[5]),
    .R4(somaR[4]), .R3(somaR[3]), .R2(somaR[2]), .R1(somaR[1]), .R0(somaR[0]), .CarryIn(1'b0));
  Multiplier8bit multiplier8bit_1 (
    .a0(multA[0]), .a1(multA[1]), .a2(multA[2]), .a3(multA[3]), .a4(multA[4]), .a5(multA[5]), .a6(multA[6]),
    .a7(multA[7]), .in_10(1'b0), .b7(multB[7]), .b6(multB[6]), .b5(multB[5]), .b4(multB[4]), .b3(multB[3]),
    .b2(multB[2]), .b1(multB[1]), .b0(multB[0]), .out_33(multOVERFLOW), .r7(multR[7]), .r6(multR[6]),
    .r5(multR[5]), .r4(multR[4]), .r3(multR[3]), .r2(multR[2]), .r1(multR[1]), .r0(multR[0]), .in_12(1'b0),
    .in_14(1'b0), .in_16(1'b0), .in_18(1'b0), .in_20(1'b0), .in_22(1'b0), .in_24(1'b0));
  Demultiplexer #(.select(3), .width(8), .enable("false")) demultiplexer_1 (
    .out0(somaA), .out1(subA), .out2(multA), .out3(demultiplexer_1_out3), .out4(demultiplexer_1_out4),
    .in({A7, A6, A5, A4, A3, A2, A1, A0}), .sel({in_17, in_18, in_19}));  // open: out5, out6, out7
  Demultiplexer #(.select(3), .width(8), .enable("false")) demultiplexer_2 (
    .out0(somaB), .out1(subB), .out2(multB), .out3(demultiplexer_2_out3), .out4(demultiplexer_2_out4),
    .in({B7, B6, B5, B4, B3, B2, B1, B0}), .sel({in_17, in_18, in_19}));  // open: out5, out6, out7
  Divisao divisao_1 (
    .A7(divA[7]), .A6(divA[6]), .A5(divA[5]), .A4(divA[4]), .A3(divA[3]), .A2(divA[2]), .A1(divA[1]),
    .A0(divA[0]), .B7(divB[7]), .B6(divB[6]), .B5(divB[5]), .B4(divB[4]), .B3(divB[3]), .B2(divB[2]),
    .B1(divB[1]), .B0(divB[0]), .Q7(divOVERFLOW), .Q6(divR[6]), .Q5(divR[5]), .Q4(divR[4]), .Q3(divR[3]),
    .Q2(divR[2]), .Q1(divR[1]), .Q0(divR[0]));
  assign divA = demultiplexer_1_out3 | demultiplexer_1_out4;  // OR_Gate or_1, 8 bits wide
  assign divB = demultiplexer_2_out3 | demultiplexer_2_out4;  // OR_Gate or_2, 8 bits wide
  subtrator_8bit subtrator_8bit_1 (
    .over(SINAL), .A7(subA[7]), .B7(subB[7]), .A6(subA[6]), .B6(subB[6]), .A5(subA[5]), .B5(subB[5]),
    .A4(subA[4]), .B4(subB[4]), .A3(subA[3]), .B3(subB[3]), .A2(subA[2]), .B2(subB[2]), .A1(subA[1]),
    .B1(subB[1]), .A0(subA[0]), .B0(subB[0]), .R7(subR[7]), .R6(subR[6]), .R5(subR[5]), .R4(subR[4]),
    .R3(subR[3]), .R2(subR[2]), .R1(subR[1]), .R0(subR[0]), .carryIn(1'b0));
  Multiplexer #(.select(3), .width(8), .enable("false")) multiplexer_1 (
    .in0(somaR), .in1(subR), .in2(multR), .in3({divOVERFLOW, divR}), .in4(Resto),
    .out({R7, R6, R5, R4, R3, R2, R1, R0}), .sel({in_17, in_18, in_19}));  // open: in5, in6, in7
  or or_3 (out_28, somaOVERFLOW, SINAL, SINALresto, multOVERFLOW, divOVERFLOW);

  // Other names for the same wires on the sheet: divR[7] = divOVERFLOW; OVERFLOW = out_28;
  //   S[2:0] = {in_17, in_18, in_19}

  // Notes on the sheet:
  //   SELECAO da OPERACAO
  //   SOMA
  //   MULTIPLICACAO
  //   RESTO
  //   DIVISAO
  //   000 - SOMA
  //   001 - SUBTRACAO
  //   010 - MULTIPLICACAO
  //   011 - DIVISAO
  //   100 - RESTO
  //   carryIn
  //   carryIn
  //   SUBTRACAO
  //   DIVISAO
  //   carryIn
endmodule

module halfAdder (
  input  in_1,
  input  in_2,
  output out_3,
  output out_4
);

  xor xor_1 (out_3, in_1, in_2);
  and and_1 (out_4, in_1, in_2);
endmodule

module FullAdder (
  input  in_1,
  input  in_2,
  input  carry,
  output out_4,
  output out_5
);

  wire halfadder_1_out_3, halfadder_1_out_4, halfadder_2_out_4;

  or or_1 (out_4, halfadder_1_out_4, halfadder_2_out_4);
  halfAdder halfadder_1 (.in_1(in_2), .in_2(in_1), .out_3(halfadder_1_out_3), .out_4(halfadder_1_out_4));
  halfAdder halfadder_2 (.in_1(halfadder_1_out_3), .in_2(carry), .out_3(out_5), .out_4(halfadder_2_out_4));
endmodule

module Adder8Bit (
  input  A0,
  input  A1,
  input  A2,
  input  A3,
  input  A4,
  input  A5,
  input  A6,
  input  A7,
  input  B0,
  input  B1,
  input  B2,
  input  B3,
  input  B4,
  input  B5,
  input  B6,
  input  B7,
  input  CarryIn,
  output OVERFLOW,
  output R7,
  output R6,
  output R5,
  output R4,
  output R3,
  output R2,
  output R1,
  output R0
);

  wire fulladder_2_out_4, fulladder_3_out_4, fulladder_4_out_4, fulladder_5_out_4, fulladder_6_out_4,
       fulladder_7_out_4, fulladder_8_out_4;

  FullAdder fulladder_1 (.in_1(B7), .in_2(A7), .out_4(OVERFLOW), .out_5(R7), .carry(fulladder_2_out_4));
  FullAdder fulladder_2 (.in_1(B6), .in_2(A6), .out_4(fulladder_2_out_4), .out_5(R6), .carry(fulladder_3_out_4));
  FullAdder fulladder_3 (.in_1(B5), .in_2(A5), .out_4(fulladder_3_out_4), .out_5(R5), .carry(fulladder_4_out_4));
  FullAdder fulladder_4 (.in_1(B4), .in_2(A4), .out_4(fulladder_4_out_4), .out_5(R4), .carry(fulladder_5_out_4));
  FullAdder fulladder_5 (.in_1(B3), .in_2(A3), .out_4(fulladder_5_out_4), .out_5(R3), .carry(fulladder_6_out_4));
  FullAdder fulladder_6 (.in_1(B2), .in_2(A2), .out_4(fulladder_6_out_4), .out_5(R2), .carry(fulladder_7_out_4));
  FullAdder fulladder_7 (.in_1(B1), .in_2(A1), .out_4(fulladder_7_out_4), .out_5(R1), .carry(fulladder_8_out_4));
  FullAdder fulladder_8 (.in_1(B0), .in_2(A0), .out_4(fulladder_8_out_4), .out_5(R0), .carry(CarryIn));
endmodule

module semi_subtrator (
  input  in_1,
  input  in_2,
  output out_3,
  output out_4
);

  wire not_1_out;

  not not_1 (not_1_out, in_1);
  and and_1 (out_3, not_1_out, in_2);
  xor xor_1 (out_4, in_1, in_2);
endmodule

module \subtrator_básico  (
  input  in_1,
  input  in_2,
  input  in_3,
  output out_4,
  output out_5
);

  wire semi_subtrator_1_out_3, semi_subtrator_1_out_4, semi_subtrator_2_out_3;

  semi_subtrator semi_subtrator_1 (
    .in_1(in_1), .in_2(in_2), .out_3(semi_subtrator_1_out_3), .out_4(semi_subtrator_1_out_4));
  semi_subtrator semi_subtrator_2 (
    .in_1(semi_subtrator_1_out_4), .in_2(in_3), .out_3(semi_subtrator_2_out_3), .out_4(out_5));
  or or_1 (out_4, semi_subtrator_1_out_3, semi_subtrator_2_out_3);
endmodule

module subtrator_8bit (
  input  A7,
  input  A6,
  input  A5,
  input  A4,
  input  A3,
  input  A2,
  input  A1,
  input  A0,
  input  B7,
  input  B6,
  input  B5,
  input  B4,
  input  B3,
  input  B2,
  input  B1,
  input  B0,
  input  carryIn,
  output over,
  output R7,
  output R6,
  output R5,
  output R4,
  output R3,
  output R2,
  output R1,
  output R0
);

  wire \subtrator_básico_2_out_4 , \subtrator_básico_3_out_4 , \subtrator_básico_4_out_4 ,
       \subtrator_básico_5_out_4 , \subtrator_básico_6_out_4 , \subtrator_básico_7_out_4 ,
       \subtrator_básico_8_out_4 ;

  \subtrator_básico  \subtrator_básico_1  (
    .in_1(A7), .in_2(B7), .out_4(over), .out_5(R7), .in_3(\subtrator_básico_2_out_4 ));
  \subtrator_básico  \subtrator_básico_2  (
    .in_1(A6), .in_2(B6), .out_4(\subtrator_básico_2_out_4 ), .out_5(R6), .in_3(\subtrator_básico_3_out_4 ));
  \subtrator_básico  \subtrator_básico_3  (
    .in_1(A5), .in_2(B5), .out_4(\subtrator_básico_3_out_4 ), .out_5(R5), .in_3(\subtrator_básico_4_out_4 ));
  \subtrator_básico  \subtrator_básico_4  (
    .in_1(A4), .in_2(B4), .out_4(\subtrator_básico_4_out_4 ), .out_5(R4), .in_3(\subtrator_básico_5_out_4 ));
  \subtrator_básico  \subtrator_básico_5  (
    .in_1(A3), .in_2(B3), .out_4(\subtrator_básico_5_out_4 ), .out_5(R3), .in_3(\subtrator_básico_6_out_4 ));
  \subtrator_básico  \subtrator_básico_6  (
    .in_1(A2), .in_2(B2), .out_4(\subtrator_básico_6_out_4 ), .out_5(R2), .in_3(\subtrator_básico_7_out_4 ));
  \subtrator_básico  \subtrator_básico_7  (
    .in_1(A1), .in_2(B1), .out_4(\subtrator_básico_7_out_4 ), .out_5(R1), .in_3(\subtrator_básico_8_out_4 ));
  \subtrator_básico  \subtrator_básico_8  (
    .in_1(A0), .in_2(B0), .out_4(\subtrator_básico_8_out_4 ), .out_5(R0), .in_3(carryIn));
endmodule

module Multiplier8bit (
  input  b7,
  input  b6,
  input  b5,
  input  b4,
  input  b3,
  input  b2,
  input  b1,
  input  b0,
  input  a0,
  input  in_10,
  input  a1,
  input  in_12,
  input  a2,
  input  in_14,
  input  a3,
  input  in_16,
  input  a4,
  input  in_18,
  input  a5,
  input  in_20,
  input  a6,
  input  in_22,
  input  a7,
  input  in_24,
  output r7,
  output r6,
  output r5,
  output r4,
  output r3,
  output r2,
  output r1,
  output r0,
  output out_33
);

  wire _7b7_out, a0b1_out, a0b2_out, a0b3_out, a0b4_out, a0b5_out, a0b6_out, a0b7_out, a1b0_out, a1b1_out,
       a1b2_out, a1b3_out, a1b4_out, a1b5_out, a1b6_out, a1b7_out, a2b0_out, a2b1_out, a2b2_out, a2b3_out,
       a2b4_out, a2b5_out, a2b6_out, a2b7_out, a3b0_out, a3b1_out, a3b2_out, a3b3_out, a3b4_out, a3b5_out,
       a3b6_out, a3b7_out, a4b0_out, a4b1_out, a4b2_out, a4b3_out, a4b4_out, a4b5_out, a4b6_out, a4b7_out,
       a5b0_out, a5b1_out, a5b2_out, a5b3_out, a5b4_out, a5b5a_out, a5b6_out, a5b7_out, a6b0_out, a6b1_out,
       a6b2_out, a6b3_out, a6b4_out, a6b5_out, a6b6_out, a6b7_out, a7b0_out, a7b1_out, a7b2_out, a7b3_out,
       a7b4_out, a7b5_out, a7b6_out, fulladder_1_out_4, fulladder_1_out_5, fulladder_2_out_4,
       fulladder_2_out_5, fulladder_3_out_4, fulladder_3_out_5, fulladder_4_out_4, fulladder_4_out_5,
       fulladder_5_out_4, fulladder_5_out_5, fulladder_6_out_4, fulladder_6_out_5, fulladder_7_out_4,
       fulladder_7_out_5, fulladder_8_out_4, fulladder_8_out_5, fulladder_9_out_4, fulladder_9_out_5,
       fulladder_10_out_4, fulladder_10_out_5, fulladder_11_out_4, fulladder_11_out_5, fulladder_12_out_4,
       fulladder_12_out_5, fulladder_13_out_4, fulladder_13_out_5, fulladder_14_out_4, fulladder_14_out_5,
       fulladder_15_out_4, fulladder_15_out_5, fulladder_16_out_4, fulladder_16_out_5, fulladder_17_out_4,
       fulladder_17_out_5, fulladder_18_out_4, fulladder_18_out_5, fulladder_19_out_4, fulladder_19_out_5,
       fulladder_20_out_4, fulladder_20_out_5, fulladder_21_out_4, fulladder_21_out_5, fulladder_22_out_4,
       fulladder_22_out_5, fulladder_23_out_4, fulladder_23_out_5, fulladder_24_out_4, fulladder_24_out_5,
       fulladder_25_out_4, fulladder_25_out_5, fulladder_26_out_4, fulladder_26_out_5, fulladder_27_out_4,
       fulladder_27_out_5, fulladder_28_out_4, fulladder_28_out_5, fulladder_29_out_4, fulladder_29_out_5,
       fulladder_30_out_4, fulladder_30_out_5, fulladder_31_out_4, fulladder_31_out_5, fulladder_32_out_4,
       fulladder_32_out_5, fulladder_33_out_4, fulladder_33_out_5, fulladder_34_out_4, fulladder_34_out_5,
       fulladder_35_out_4, fulladder_36_out_4, fulladder_36_out_5, fulladder_37_out_4, fulladder_37_out_5,
       fulladder_38_out_4, fulladder_38_out_5, fulladder_39_out_4, fulladder_39_out_5, fulladder_40_out_4,
       fulladder_40_out_5, fulladder_41_out_4, fulladder_42_out_4, fulladder_42_out_5, fulladder_43_out_4,
       fulladder_43_out_5, fulladder_44_out_4, fulladder_44_out_5, fulladder_45_out_4, fulladder_45_out_5,
       fulladder_46_out_4, fulladder_46_out_5, fulladder_47_out_4, fulladder_47_out_5, fulladder_48_out_4,
       fulladder_48_out_5, fulladder_49_out_4, fulladder_50_out_4, fulladder_51_out_4, fulladder_51_out_5,
       fulladder_52_out_4, fulladder_52_out_5, fulladder_53_out_4, fulladder_54_out_4, fulladder_54_out_5,
       fulladder_55_out_4, fulladder_56_out_4;

  and _7b7 (_7b7_out, a7, b7);
  and a6b7 (a6b7_out, a6, b7);
  and a7b6 (a7b6_out, a7, b6);
  FullAdder fulladder_1 (
    .in_1(_7b7_out), .in_2(fulladder_4_out_4), .out_4(fulladder_1_out_4), .out_5(fulladder_1_out_5),
    .carry(fulladder_6_out_4));
  and a5b7 (a5b7_out, a5, b7);
  FullAdder fulladder_2 (
    .in_1(a5b7_out), .in_2(fulladder_7_out_4), .out_4(fulladder_2_out_4), .out_5(fulladder_2_out_5),
    .carry(fulladder_8_out_4));
  and a6b6 (a6b6_out, a6, b6);
  FullAdder fulladder_3 (
    .in_1(a6b6_out), .in_2(fulladder_2_out_5), .out_4(fulladder_3_out_4), .out_5(fulladder_3_out_5),
    .carry(fulladder_9_out_4));
  FullAdder fulladder_4 (
    .in_1(a6b7_out), .in_2(fulladder_2_out_4), .out_4(fulladder_4_out_4), .out_5(fulladder_4_out_5),
    .carry(fulladder_3_out_4));
  and a7b5 (a7b5_out, a7, b5);
  FullAdder fulladder_5 (
    .in_1(a7b5_out), .in_2(fulladder_3_out_5), .out_4(fulladder_5_out_4), .out_5(fulladder_5_out_5),
    .carry(fulladder_10_out_4));
  FullAdder fulladder_6 (
    .in_1(a7b6_out), .in_2(fulladder_4_out_5), .out_4(fulladder_6_out_4), .out_5(fulladder_6_out_5),
    .carry(fulladder_5_out_4));
  and a4b7 (a4b7_out, a4, b7);
  FullAdder fulladder_7 (
    .in_1(a4b7_out), .in_2(fulladder_11_out_4), .out_4(fulladder_7_out_4), .out_5(fulladder_7_out_5),
    .carry(fulladder_12_out_4));
  and a5b6 (a5b6_out, a5, b6);
  FullAdder fulladder_8 (
    .in_1(a5b6_out), .in_2(fulladder_7_out_5), .out_4(fulladder_8_out_4), .out_5(fulladder_8_out_5),
    .carry(fulladder_13_out_4));
  and a6b5 (a6b5_out, a6, b5);
  FullAdder fulladder_9 (
    .in_1(a6b5_out), .in_2(fulladder_8_out_5), .out_4(fulladder_9_out_4), .out_5(fulladder_9_out_5),
    .carry(fulladder_14_out_4));
  and a7b4 (a7b4_out, a7, b4);
  FullAdder fulladder_10 (
    .in_1(a7b4_out), .in_2(fulladder_9_out_5), .out_4(fulladder_10_out_4), .out_5(fulladder_10_out_5),
    .carry(fulladder_15_out_4));
  and a2b7 (a2b7_out, a2, b7);
  and a3b7 (a3b7_out, a3, b7);
  and a3b6 (a3b6_out, a3, b6);
  FullAdder fulladder_11 (
    .in_1(a3b7_out), .in_2(fulladder_16_out_4), .out_4(fulladder_11_out_4), .out_5(fulladder_11_out_5),
    .carry(fulladder_17_out_4));
  and a4b6 (a4b6_out, a4, b6);
  and a4b5 (a4b5_out, a4, b5);
  FullAdder fulladder_12 (
    .in_1(a4b6_out), .in_2(fulladder_11_out_5), .out_4(fulladder_12_out_4), .out_5(fulladder_12_out_5),
    .carry(fulladder_18_out_4));
  and a5b5a (a5b5a_out, a5, b5);
  and a5b4 (a5b4_out, a5, b4);
  FullAdder fulladder_13 (
    .in_1(a5b5a_out), .in_2(fulladder_12_out_5), .out_4(fulladder_13_out_4), .out_5(fulladder_13_out_5),
    .carry(fulladder_19_out_4));
  and a6b3 (a6b3_out, a6, b3);
  and a6b4 (a6b4_out, a6, b4);
  FullAdder fulladder_14 (
    .in_1(a6b4_out), .in_2(fulladder_13_out_5), .out_4(fulladder_14_out_4), .out_5(fulladder_14_out_5),
    .carry(fulladder_20_out_4));
  and a7b2 (a7b2_out, a7, b2);
  and a7b3 (a7b3_out, a7, b3);
  FullAdder fulladder_15 (
    .in_1(a7b3_out), .in_2(fulladder_14_out_5), .out_4(fulladder_15_out_4), .out_5(fulladder_15_out_5),
    .carry(fulladder_21_out_4));
  and a1b7 (a1b7_out, a1, b7);
  and a2b6 (a2b6_out, a2, b6);
  FullAdder fulladder_16 (
    .in_1(a2b7_out), .in_2(fulladder_22_out_4), .out_4(fulladder_16_out_4), .out_5(fulladder_16_out_5),
    .carry(fulladder_23_out_4));
  and a3b5 (a3b5_out, a3, b5);
  FullAdder fulladder_17 (
    .in_1(a3b6_out), .in_2(fulladder_16_out_5), .out_4(fulladder_17_out_4), .out_5(fulladder_17_out_5),
    .carry(fulladder_24_out_4));
  and a4b4 (a4b4_out, a4, b4);
  FullAdder fulladder_18 (
    .in_1(a4b5_out), .in_2(fulladder_17_out_5), .out_4(fulladder_18_out_4), .out_5(fulladder_18_out_5),
    .carry(fulladder_25_out_4));
  and a5b3 (a5b3_out, a5, b3);
  FullAdder fulladder_19 (
    .in_1(a5b4_out), .in_2(fulladder_18_out_5), .out_4(fulladder_19_out_4), .out_5(fulladder_19_out_5),
    .carry(fulladder_26_out_4));
  and a6b2 (a6b2_out, a6, b2);
  FullAdder fulladder_20 (
    .in_1(a6b3_out), .in_2(fulladder_19_out_5), .out_4(fulladder_20_out_4), .out_5(fulladder_20_out_5),
    .carry(fulladder_27_out_4));
  and a7b1 (a7b1_out, a7, b1);
  FullAdder fulladder_21 (
    .in_1(a7b2_out), .in_2(fulladder_20_out_5), .out_4(fulladder_21_out_4), .out_5(fulladder_21_out_5),
    .carry(fulladder_28_out_4));
  or or_1 (out_33, fulladder_1_out_4, fulladder_1_out_5, fulladder_6_out_5, fulladder_5_out_5, fulladder_10_out_5, fulladder_15_out_5, fulladder_21_out_5, fulladder_28_out_5);
  and a1b6 (a1b6_out, a1, b6);
  FullAdder fulladder_22 (
    .in_1(a1b7_out), .in_2(in_10), .out_4(fulladder_22_out_4), .out_5(fulladder_22_out_5),
    .carry(fulladder_29_out_4));
  and a2b5 (a2b5_out, a2, b5);
  FullAdder fulladder_23 (
    .in_1(a2b6_out), .in_2(fulladder_22_out_5), .out_4(fulladder_23_out_4), .out_5(fulladder_23_out_5),
    .carry(fulladder_30_out_4));
  and a3b4 (a3b4_out, a3, b4);
  FullAdder fulladder_24 (
    .in_1(a3b5_out), .in_2(fulladder_23_out_5), .out_4(fulladder_24_out_4), .out_5(fulladder_24_out_5),
    .carry(fulladder_31_out_4));
  and a4b3 (a4b3_out, a4, b3);
  FullAdder fulladder_25 (
    .in_1(a4b4_out), .in_2(fulladder_24_out_5), .out_4(fulladder_25_out_4), .out_5(fulladder_25_out_5),
    .carry(fulladder_32_out_4));
  and a5b2 (a5b2_out, a5, b2);
  FullAdder fulladder_26 (
    .in_1(a5b3_out), .in_2(fulladder_25_out_5), .out_4(fulladder_26_out_4), .out_5(fulladder_26_out_5),
    .carry(fulladder_33_out_4));
  and a6b1 (a6b1_out, a6, b1);
  FullAdder fulladder_27 (
    .in_1(a6b2_out), .in_2(fulladder_26_out_5), .out_4(fulladder_27_out_4), .out_5(fulladder_27_out_5),
    .carry(fulladder_34_out_4));
  and a7b0 (a7b0_out, a7, b0);
  FullAdder fulladder_28 (
    .in_1(a7b1_out), .in_2(fulladder_27_out_5), .out_4(fulladder_28_out_4), .out_5(fulladder_28_out_5),
    .carry(fulladder_35_out_4));
  and a0b7 (a0b7_out, a0, b7);
  and a1b5 (a1b5_out, a1, b5);
  FullAdder fulladder_29 (
    .in_1(a1b6_out), .in_2(a0b7_out), .out_4(fulladder_29_out_4), .out_5(fulladder_29_out_5),
    .carry(fulladder_36_out_4));
  and a2b4 (a2b4_out, a2, b4);
  FullAdder fulladder_30 (
    .in_1(a2b5_out), .in_2(fulladder_29_out_5), .out_4(fulladder_30_out_4), .out_5(fulladder_30_out_5),
    .carry(fulladder_37_out_4));
  and a3b3 (a3b3_out, a3, b3);
  FullAdder fulladder_31 (
    .in_1(a3b4_out), .in_2(fulladder_30_out_5), .out_4(fulladder_31_out_4), .out_5(fulladder_31_out_5),
    .carry(fulladder_38_out_4));
  and a4b2 (a4b2_out, a4, b2);
  FullAdder fulladder_32 (
    .in_1(a4b3_out), .in_2(fulladder_31_out_5), .out_4(fulladder_32_out_4), .out_5(fulladder_32_out_5),
    .carry(fulladder_39_out_4));
  and a5b1 (a5b1_out, a5, b1);
  FullAdder fulladder_33 (
    .in_1(a5b2_out), .in_2(fulladder_32_out_5), .out_4(fulladder_33_out_4), .out_5(fulladder_33_out_5),
    .carry(fulladder_40_out_4));
  and a6b0 (a6b0_out, a6, b0);
  FullAdder fulladder_34 (
    .in_1(a6b1_out), .in_2(fulladder_33_out_5), .out_4(fulladder_34_out_4), .out_5(fulladder_34_out_5),
    .carry(fulladder_41_out_4));
  FullAdder fulladder_35 (
    .in_1(a7b0_out), .in_2(fulladder_34_out_5), .out_4(fulladder_35_out_4), .out_5(r7), .carry(in_24));
  and a0b5 (a0b5_out, a0, b5);
  and a0b6 (a0b6_out, a0, b6);
  and a1b4 (a1b4_out, a1, b4);
  FullAdder fulladder_36 (
    .in_1(a1b5_out), .in_2(a0b6_out), .out_4(fulladder_36_out_4), .out_5(fulladder_36_out_5),
    .carry(fulladder_43_out_4));
  and a2b3 (a2b3_out, a2, b3);
  FullAdder fulladder_37 (
    .in_1(a2b4_out), .in_2(fulladder_36_out_5), .out_4(fulladder_37_out_4), .out_5(fulladder_37_out_5),
    .carry(fulladder_45_out_4));
  and a3b2 (a3b2_out, a3, b2);
  FullAdder fulladder_38 (
    .in_1(a3b3_out), .in_2(fulladder_37_out_5), .out_4(fulladder_38_out_4), .out_5(fulladder_38_out_5),
    .carry(fulladder_46_out_4));
  and a4b1 (a4b1_out, a4, b1);
  FullAdder fulladder_39 (
    .in_1(a4b2_out), .in_2(fulladder_38_out_5), .out_4(fulladder_39_out_4), .out_5(fulladder_39_out_5),
    .carry(fulladder_48_out_4));
  and a5b0 (a5b0_out, a5, b0);
  FullAdder fulladder_40 (
    .in_1(a5b1_out), .in_2(fulladder_39_out_5), .out_4(fulladder_40_out_4), .out_5(fulladder_40_out_5),
    .carry(fulladder_50_out_4));
  FullAdder fulladder_41 (
    .in_1(a6b0_out), .in_2(fulladder_40_out_5), .out_4(fulladder_41_out_4), .out_5(r6), .carry(in_22));
  and a0b4 (a0b4_out, a0, b4);
  and a1b3 (a1b3_out, a1, b3);
  FullAdder fulladder_42 (
    .in_1(a1b3_out), .in_2(a0b4_out), .out_4(fulladder_42_out_4), .out_5(fulladder_42_out_5),
    .carry(fulladder_51_out_4));
  FullAdder fulladder_43 (
    .in_1(a1b4_out), .in_2(a0b5_out), .out_4(fulladder_43_out_4), .out_5(fulladder_43_out_5),
    .carry(fulladder_42_out_4));
  and a2b2 (a2b2_out, a2, b2);
  FullAdder fulladder_44 (
    .in_1(a2b2_out), .in_2(fulladder_42_out_5), .out_4(fulladder_44_out_4), .out_5(fulladder_44_out_5),
    .carry(fulladder_52_out_4));
  FullAdder fulladder_45 (
    .in_1(a2b3_out), .in_2(fulladder_43_out_5), .out_4(fulladder_45_out_4), .out_5(fulladder_45_out_5),
    .carry(fulladder_44_out_4));
  and a3b1 (a3b1_out, a3, b1);
  FullAdder fulladder_46 (
    .in_1(a3b2_out), .in_2(fulladder_45_out_5), .out_4(fulladder_46_out_4), .out_5(fulladder_46_out_5),
    .carry(fulladder_47_out_4));
  FullAdder fulladder_47 (
    .in_1(a3b1_out), .in_2(fulladder_44_out_5), .out_4(fulladder_47_out_4), .out_5(fulladder_47_out_5),
    .carry(fulladder_53_out_4));
  and a4b0 (a4b0_out, a4, b0);
  FullAdder fulladder_48 (
    .in_1(a4b1_out), .in_2(fulladder_46_out_5), .out_4(fulladder_48_out_4), .out_5(fulladder_48_out_5),
    .carry(fulladder_49_out_4));
  FullAdder fulladder_49 (
    .in_1(a4b0_out), .in_2(fulladder_47_out_5), .out_4(fulladder_49_out_4), .out_5(r4), .carry(in_18));
  FullAdder fulladder_50 (
    .in_1(a5b0_out), .in_2(fulladder_48_out_5), .out_4(fulladder_50_out_4), .out_5(r5), .carry(in_20));
  and a0b3 (a0b3_out, a0, b3);
  and a1b2 (a1b2_out, a1, b2);
  FullAdder fulladder_51 (
    .in_1(a1b2_out), .in_2(a0b3_out), .out_4(fulladder_51_out_4), .out_5(fulladder_51_out_5),
    .carry(fulladder_54_out_4));
  and a2b1 (a2b1_out, a2, b1);
  FullAdder fulladder_52 (
    .in_1(a2b1_out), .in_2(fulladder_51_out_5), .out_4(fulladder_52_out_4), .out_5(fulladder_52_out_5),
    .carry(fulladder_55_out_4));
  and a3b0 (a3b0_out, a3, b0);
  FullAdder fulladder_53 (
    .in_1(a3b0_out), .in_2(fulladder_52_out_5), .out_4(fulladder_53_out_4), .out_5(r3), .carry(in_16));
  and a0b2 (a0b2_out, a0, b2);
  and a1b0 (a1b0_out, a1, b0);
  and a1b1 (a1b1_out, a1, b1);
  FullAdder fulladder_54 (
    .in_1(a1b1_out), .in_2(a0b2_out), .out_4(fulladder_54_out_4), .out_5(fulladder_54_out_5),
    .carry(fulladder_56_out_4));
  and a2b0 (a2b0_out, a2, b0);
  FullAdder fulladder_55 (
    .in_1(a2b0_out), .in_2(fulladder_54_out_5), .out_4(fulladder_55_out_4), .out_5(r2), .carry(in_14));
  and a0b1 (a0b1_out, a0, b1);
  FullAdder fulladder_56 (.in_1(a1b0_out), .in_2(a0b1_out), .out_4(fulladder_56_out_4), .out_5(r1), .carry(in_12));
  and a0b0 (r0, a0, b0);
endmodule

module CAS___controlled_add_subtract (
  input  remainder_in,
  input  T,
  input  divisor,
  input  carry_in,
  output carry_out,
  output remainder_out
);

  wire xor_1_out;

  xor xor_1 (xor_1_out, T, divisor);
  FullAdder fulladder_1 (
    .in_1(xor_1_out), .in_2(remainder_in), .out_4(carry_out), .out_5(remainder_out), .carry(carry_in));
endmodule

module Resto (
  input  A7,
  input  A6,
  input  A5,
  input  A4,
  input  A3,
  input  A2,
  input  A1,
  input  A0,
  input  B7,
  input  B6,
  input  B5,
  input  B4,
  input  B3,
  input  B2,
  input  B1,
  input  B0,
  input  Q7,
  input  Q6,
  input  Q5,
  input  Q4,
  input  Q3,
  input  Q2,
  input  Q1,
  input  Q0,
  output R7,
  output R6,
  output R5,
  output R4,
  output R3,
  output R2,
  output R1,
  output R0,
  output sinal
);

  wire multOVERFLOW;
  wire [7:0] BQ;

  Multiplier8bit multiplier8bit_1 (
    .a0(B0), .a1(B1), .a2(B2), .a3(B3), .a4(B4), .a5(B5), .a6(B6), .a7(B7), .in_10(1'b0), .b7(Q7), .b6(Q6),
    .b5(Q5), .b4(Q4), .b3(Q3), .b2(Q2), .b1(Q1), .b0(Q0), .out_33(multOVERFLOW), .r7(BQ[7]), .r6(BQ[6]),
    .r5(BQ[5]), .r4(BQ[4]), .r3(BQ[3]), .r2(BQ[2]), .r1(BQ[1]), .r0(BQ[0]), .in_12(1'b0), .in_14(1'b0),
    .in_16(1'b0), .in_18(1'b0), .in_20(1'b0), .in_22(1'b0), .in_24(1'b0));
  subtrator_8bit subtrator_8bit_1 (
    .over(sinal), .A7(A7), .B7(BQ[7]), .A6(A6), .B6(BQ[6]), .A5(A5), .B5(BQ[5]), .A4(A4), .B4(BQ[4]),
    .A3(A3), .B3(BQ[3]), .A2(A2), .B2(BQ[2]), .A1(A1), .B1(BQ[1]), .A0(A0), .B0(BQ[0]), .R7(R7), .R6(R6),
    .R5(R5), .R4(R4), .R3(R3), .R2(R2), .R1(R1), .R0(R0), .carryIn(1'b0));

  // Notes on the sheet:
  //   MULTIPLICACAO
  //   carryIn
  //   SUBTRACAO
  //   carryIn
endmodule

module Divisao (
  input  A7,
  input  A6,
  input  A5,
  input  A4,
  input  A3,
  input  A2,
  input  A1,
  input  A0,
  input  B7,
  input  B6,
  input  B5,
  input  B4,
  input  B3,
  input  B2,
  input  B1,
  input  B0,
  output Q7,
  output Q6,
  output Q5,
  output Q4,
  output Q3,
  output Q2,
  output Q1,
  output Q0
);

  wire cas_controlled_add_subtract_1_carry_out, cas_controlled_add_subtract_1_remainder_out,
       cas_controlled_add_subtract_2_carry_out, cas_controlled_add_subtract_2_remainder_out,
       cas_controlled_add_subtract_3_carry_out, cas_controlled_add_subtract_3_remainder_out,
       cas_controlled_add_subtract_4_carry_out, cas_controlled_add_subtract_4_remainder_out,
       cas_controlled_add_subtract_5_carry_out, cas_controlled_add_subtract_5_remainder_out,
       cas_controlled_add_subtract_6_carry_out, cas_controlled_add_subtract_6_remainder_out,
       cas_controlled_add_subtract_7_carry_out, cas_controlled_add_subtract_7_remainder_out,
       cas_controlled_add_subtract_8_carry_out, cas_controlled_add_subtract_8_remainder_out,
       cas_controlled_add_subtract_9_carry_out, cas_controlled_add_subtract_9_remainder_out,
       cas_controlled_add_subtract_10_carry_out, cas_controlled_add_subtract_10_remainder_out,
       cas_controlled_add_subtract_11_carry_out, cas_controlled_add_subtract_11_remainder_out,
       cas_controlled_add_subtract_12_carry_out, cas_controlled_add_subtract_12_remainder_out,
       cas_controlled_add_subtract_13_carry_out, cas_controlled_add_subtract_13_remainder_out,
       cas_controlled_add_subtract_14_carry_out, cas_controlled_add_subtract_14_remainder_out,
       cas_controlled_add_subtract_15_carry_out, cas_controlled_add_subtract_15_remainder_out,
       cas_controlled_add_subtract_16_carry_out, cas_controlled_add_subtract_16_remainder_out,
       cas_controlled_add_subtract_17_carry_out, cas_controlled_add_subtract_17_remainder_out,
       cas_controlled_add_subtract_18_carry_out, cas_controlled_add_subtract_18_remainder_out,
       cas_controlled_add_subtract_19_carry_out, cas_controlled_add_subtract_19_remainder_out,
       cas_controlled_add_subtract_20_carry_out, cas_controlled_add_subtract_20_remainder_out,
       cas_controlled_add_subtract_21_carry_out, cas_controlled_add_subtract_21_remainder_out,
       cas_controlled_add_subtract_22_carry_out, cas_controlled_add_subtract_22_remainder_out,
       cas_controlled_add_subtract_23_carry_out, cas_controlled_add_subtract_23_remainder_out,
       cas_controlled_add_subtract_24_carry_out, cas_controlled_add_subtract_24_remainder_out,
       cas_controlled_add_subtract_25_carry_out, cas_controlled_add_subtract_25_remainder_out,
       cas_controlled_add_subtract_26_carry_out, cas_controlled_add_subtract_26_remainder_out,
       cas_controlled_add_subtract_27_carry_out, cas_controlled_add_subtract_27_remainder_out,
       cas_controlled_add_subtract_28_carry_out, cas_controlled_add_subtract_28_remainder_out,
       cas_controlled_add_subtract_29_carry_out, cas_controlled_add_subtract_29_remainder_out,
       cas_controlled_add_subtract_30_carry_out, cas_controlled_add_subtract_30_remainder_out,
       cas_controlled_add_subtract_31_carry_out, cas_controlled_add_subtract_31_remainder_out,
       cas_controlled_add_subtract_32_carry_out, cas_controlled_add_subtract_32_remainder_out,
       cas_controlled_add_subtract_33_carry_out, cas_controlled_add_subtract_33_remainder_out,
       cas_controlled_add_subtract_34_carry_out, cas_controlled_add_subtract_34_remainder_out,
       cas_controlled_add_subtract_35_carry_out, cas_controlled_add_subtract_35_remainder_out,
       cas_controlled_add_subtract_36_carry_out, cas_controlled_add_subtract_36_remainder_out,
       cas_controlled_add_subtract_37_carry_out, cas_controlled_add_subtract_37_remainder_out,
       cas_controlled_add_subtract_38_carry_out, cas_controlled_add_subtract_38_remainder_out,
       cas_controlled_add_subtract_39_carry_out, cas_controlled_add_subtract_39_remainder_out,
       cas_controlled_add_subtract_40_carry_out, cas_controlled_add_subtract_40_remainder_out,
       cas_controlled_add_subtract_41_carry_out, cas_controlled_add_subtract_41_remainder_out,
       cas_controlled_add_subtract_42_carry_out, cas_controlled_add_subtract_42_remainder_out,
       cas_controlled_add_subtract_43_carry_out, cas_controlled_add_subtract_43_remainder_out,
       cas_controlled_add_subtract_44_carry_out, cas_controlled_add_subtract_44_remainder_out,
       cas_controlled_add_subtract_45_carry_out, cas_controlled_add_subtract_45_remainder_out,
       cas_controlled_add_subtract_46_carry_out, cas_controlled_add_subtract_46_remainder_out,
       cas_controlled_add_subtract_47_carry_out, cas_controlled_add_subtract_47_remainder_out,
       cas_controlled_add_subtract_48_carry_out, cas_controlled_add_subtract_48_remainder_out,
       cas_controlled_add_subtract_49_carry_out, cas_controlled_add_subtract_49_remainder_out,
       cas_controlled_add_subtract_50_carry_out, cas_controlled_add_subtract_50_remainder_out,
       cas_controlled_add_subtract_51_carry_out, cas_controlled_add_subtract_51_remainder_out,
       cas_controlled_add_subtract_52_carry_out, cas_controlled_add_subtract_52_remainder_out,
       cas_controlled_add_subtract_53_carry_out, cas_controlled_add_subtract_53_remainder_out,
       cas_controlled_add_subtract_54_carry_out, cas_controlled_add_subtract_54_remainder_out,
       cas_controlled_add_subtract_55_carry_out, cas_controlled_add_subtract_55_remainder_out,
       cas_controlled_add_subtract_56_carry_out, cas_controlled_add_subtract_56_remainder_out,
       cas_controlled_add_subtract_57_carry_out, cas_controlled_add_subtract_57_remainder_out,
       cas_controlled_add_subtract_58_carry_out, cas_controlled_add_subtract_58_remainder_out,
       cas_controlled_add_subtract_59_carry_out, cas_controlled_add_subtract_59_remainder_out,
       cas_controlled_add_subtract_60_carry_out, cas_controlled_add_subtract_60_remainder_out,
       cas_controlled_add_subtract_61_carry_out, cas_controlled_add_subtract_61_remainder_out,
       cas_controlled_add_subtract_62_carry_out, cas_controlled_add_subtract_62_remainder_out,
       cas_controlled_add_subtract_63_carry_out, cas_controlled_add_subtract_63_remainder_out,
       cas_controlled_add_subtract_64_carry_out, cas_controlled_add_subtract_64_remainder_out, not_1_out;

  not not_1 (not_1_out, 1'b0);
  CAS___controlled_add_subtract cas_controlled_add_subtract_1 (
    .carry_out(cas_controlled_add_subtract_1_carry_out), .T(not_1_out), .remainder_in(1'b0), .divisor(B7),
    .remainder_out(cas_controlled_add_subtract_1_remainder_out),
    .carry_in(cas_controlled_add_subtract_2_carry_out));
  not not_2 (Q7, cas_controlled_add_subtract_1_remainder_out);
  CAS___controlled_add_subtract cas_controlled_add_subtract_2 (
    .carry_out(cas_controlled_add_subtract_2_carry_out), .T(not_1_out), .remainder_in(1'b0), .divisor(B6),
    .remainder_out(cas_controlled_add_subtract_2_remainder_out),
    .carry_in(cas_controlled_add_subtract_4_carry_out));
  CAS___controlled_add_subtract cas_controlled_add_subtract_3 (
    .carry_out(cas_controlled_add_subtract_3_carry_out), .T(Q7),
    .remainder_in(cas_controlled_add_subtract_2_remainder_out), .divisor(B7),
    .remainder_out(cas_controlled_add_subtract_3_remainder_out),
    .carry_in(cas_controlled_add_subtract_5_carry_out));
  not not_3 (Q6, cas_controlled_add_subtract_3_remainder_out);
  CAS___controlled_add_subtract cas_controlled_add_subtract_4 (
    .carry_out(cas_controlled_add_subtract_4_carry_out), .T(not_1_out), .remainder_in(1'b0), .divisor(B5),
    .remainder_out(cas_controlled_add_subtract_4_remainder_out),
    .carry_in(cas_controlled_add_subtract_7_carry_out));
  CAS___controlled_add_subtract cas_controlled_add_subtract_5 (
    .carry_out(cas_controlled_add_subtract_5_carry_out), .T(Q7),
    .remainder_in(cas_controlled_add_subtract_4_remainder_out), .divisor(B6),
    .remainder_out(cas_controlled_add_subtract_5_remainder_out),
    .carry_in(cas_controlled_add_subtract_8_carry_out));
  CAS___controlled_add_subtract cas_controlled_add_subtract_6 (
    .carry_out(cas_controlled_add_subtract_6_carry_out), .T(Q6),
    .remainder_in(cas_controlled_add_subtract_5_remainder_out), .divisor(B7),
    .remainder_out(cas_controlled_add_subtract_6_remainder_out),
    .carry_in(cas_controlled_add_subtract_9_carry_out));
  not not_4 (Q5, cas_controlled_add_subtract_6_remainder_out);
  CAS___controlled_add_subtract cas_controlled_add_subtract_7 (
    .carry_out(cas_controlled_add_subtract_7_carry_out), .T(not_1_out), .remainder_in(1'b0), .divisor(B4),
    .remainder_out(cas_controlled_add_subtract_7_remainder_out),
    .carry_in(cas_controlled_add_subtract_11_carry_out));
  CAS___controlled_add_subtract cas_controlled_add_subtract_8 (
    .carry_out(cas_controlled_add_subtract_8_carry_out), .T(Q7),
    .remainder_in(cas_controlled_add_subtract_7_remainder_out), .divisor(B5),
    .remainder_out(cas_controlled_add_subtract_8_remainder_out),
    .carry_in(cas_controlled_add_subtract_12_carry_out));
  CAS___controlled_add_subtract cas_controlled_add_subtract_9 (
    .carry_out(cas_controlled_add_subtract_9_carry_out), .T(Q6),
    .remainder_in(cas_controlled_add_subtract_8_remainder_out), .divisor(B6),
    .remainder_out(cas_controlled_add_subtract_9_remainder_out),
    .carry_in(cas_controlled_add_subtract_13_carry_out));
  CAS___controlled_add_subtract cas_controlled_add_subtract_10 (
    .carry_out(cas_controlled_add_subtract_10_carry_out), .T(Q5),
    .remainder_in(cas_controlled_add_subtract_9_remainder_out), .divisor(B7),
    .remainder_out(cas_controlled_add_subtract_10_remainder_out),
    .carry_in(cas_controlled_add_subtract_14_carry_out));
  not not_5 (Q4, cas_controlled_add_subtract_10_remainder_out);
  CAS___controlled_add_subtract cas_controlled_add_subtract_11 (
    .carry_out(cas_controlled_add_subtract_11_carry_out), .T(not_1_out), .remainder_in(1'b0), .divisor(B3),
    .remainder_out(cas_controlled_add_subtract_11_remainder_out),
    .carry_in(cas_controlled_add_subtract_16_carry_out));
  CAS___controlled_add_subtract cas_controlled_add_subtract_12 (
    .carry_out(cas_controlled_add_subtract_12_carry_out), .T(Q7),
    .remainder_in(cas_controlled_add_subtract_11_remainder_out), .divisor(B4),
    .remainder_out(cas_controlled_add_subtract_12_remainder_out),
    .carry_in(cas_controlled_add_subtract_17_carry_out));
  CAS___controlled_add_subtract cas_controlled_add_subtract_13 (
    .carry_out(cas_controlled_add_subtract_13_carry_out), .T(Q6),
    .remainder_in(cas_controlled_add_subtract_12_remainder_out), .divisor(B5),
    .remainder_out(cas_controlled_add_subtract_13_remainder_out),
    .carry_in(cas_controlled_add_subtract_18_carry_out));
  CAS___controlled_add_subtract cas_controlled_add_subtract_14 (
    .carry_out(cas_controlled_add_subtract_14_carry_out), .T(Q5),
    .remainder_in(cas_controlled_add_subtract_13_remainder_out), .divisor(B6),
    .remainder_out(cas_controlled_add_subtract_14_remainder_out),
    .carry_in(cas_controlled_add_subtract_19_carry_out));
  CAS___controlled_add_subtract cas_controlled_add_subtract_15 (
    .carry_out(cas_controlled_add_subtract_15_carry_out), .T(Q4),
    .remainder_in(cas_controlled_add_subtract_14_remainder_out), .divisor(B7),
    .remainder_out(cas_controlled_add_subtract_15_remainder_out),
    .carry_in(cas_controlled_add_subtract_20_carry_out));
  not not_6 (Q3, cas_controlled_add_subtract_15_remainder_out);
  CAS___controlled_add_subtract cas_controlled_add_subtract_16 (
    .carry_out(cas_controlled_add_subtract_16_carry_out), .T(not_1_out), .remainder_in(1'b0), .divisor(B2),
    .remainder_out(cas_controlled_add_subtract_16_remainder_out),
    .carry_in(cas_controlled_add_subtract_22_carry_out));
  CAS___controlled_add_subtract cas_controlled_add_subtract_17 (
    .carry_out(cas_controlled_add_subtract_17_carry_out), .T(Q7),
    .remainder_in(cas_controlled_add_subtract_16_remainder_out), .divisor(B3),
    .remainder_out(cas_controlled_add_subtract_17_remainder_out),
    .carry_in(cas_controlled_add_subtract_23_carry_out));
  CAS___controlled_add_subtract cas_controlled_add_subtract_18 (
    .carry_out(cas_controlled_add_subtract_18_carry_out), .T(Q6),
    .remainder_in(cas_controlled_add_subtract_17_remainder_out), .divisor(B4),
    .remainder_out(cas_controlled_add_subtract_18_remainder_out),
    .carry_in(cas_controlled_add_subtract_24_carry_out));
  CAS___controlled_add_subtract cas_controlled_add_subtract_19 (
    .carry_out(cas_controlled_add_subtract_19_carry_out), .T(Q5),
    .remainder_in(cas_controlled_add_subtract_18_remainder_out), .divisor(B5),
    .remainder_out(cas_controlled_add_subtract_19_remainder_out),
    .carry_in(cas_controlled_add_subtract_25_carry_out));
  CAS___controlled_add_subtract cas_controlled_add_subtract_20 (
    .carry_out(cas_controlled_add_subtract_20_carry_out), .T(Q4),
    .remainder_in(cas_controlled_add_subtract_19_remainder_out), .divisor(B6),
    .remainder_out(cas_controlled_add_subtract_20_remainder_out),
    .carry_in(cas_controlled_add_subtract_26_carry_out));
  CAS___controlled_add_subtract cas_controlled_add_subtract_21 (
    .carry_out(cas_controlled_add_subtract_21_carry_out), .T(Q3),
    .remainder_in(cas_controlled_add_subtract_20_remainder_out), .divisor(B7),
    .remainder_out(cas_controlled_add_subtract_21_remainder_out),
    .carry_in(cas_controlled_add_subtract_27_carry_out));
  not not_7 (Q2, cas_controlled_add_subtract_21_remainder_out);
  CAS___controlled_add_subtract cas_controlled_add_subtract_22 (
    .carry_out(cas_controlled_add_subtract_22_carry_out), .T(not_1_out), .remainder_in(1'b0), .divisor(B1),
    .remainder_out(cas_controlled_add_subtract_22_remainder_out),
    .carry_in(cas_controlled_add_subtract_29_carry_out));
  CAS___controlled_add_subtract cas_controlled_add_subtract_23 (
    .carry_out(cas_controlled_add_subtract_23_carry_out), .T(Q7),
    .remainder_in(cas_controlled_add_subtract_22_remainder_out), .divisor(B2),
    .remainder_out(cas_controlled_add_subtract_23_remainder_out),
    .carry_in(cas_controlled_add_subtract_30_carry_out));
  CAS___controlled_add_subtract cas_controlled_add_subtract_24 (
    .carry_out(cas_controlled_add_subtract_24_carry_out), .T(Q6),
    .remainder_in(cas_controlled_add_subtract_23_remainder_out), .divisor(B3),
    .remainder_out(cas_controlled_add_subtract_24_remainder_out),
    .carry_in(cas_controlled_add_subtract_31_carry_out));
  CAS___controlled_add_subtract cas_controlled_add_subtract_25 (
    .carry_out(cas_controlled_add_subtract_25_carry_out), .T(Q5),
    .remainder_in(cas_controlled_add_subtract_24_remainder_out), .divisor(B4),
    .remainder_out(cas_controlled_add_subtract_25_remainder_out),
    .carry_in(cas_controlled_add_subtract_32_carry_out));
  CAS___controlled_add_subtract cas_controlled_add_subtract_26 (
    .carry_out(cas_controlled_add_subtract_26_carry_out), .T(Q4),
    .remainder_in(cas_controlled_add_subtract_25_remainder_out), .divisor(B5),
    .remainder_out(cas_controlled_add_subtract_26_remainder_out),
    .carry_in(cas_controlled_add_subtract_33_carry_out));
  CAS___controlled_add_subtract cas_controlled_add_subtract_27 (
    .carry_out(cas_controlled_add_subtract_27_carry_out), .T(Q3),
    .remainder_in(cas_controlled_add_subtract_26_remainder_out), .divisor(B6),
    .remainder_out(cas_controlled_add_subtract_27_remainder_out),
    .carry_in(cas_controlled_add_subtract_34_carry_out));
  CAS___controlled_add_subtract cas_controlled_add_subtract_28 (
    .carry_out(cas_controlled_add_subtract_28_carry_out), .T(Q2),
    .remainder_in(cas_controlled_add_subtract_27_remainder_out), .divisor(B7),
    .remainder_out(cas_controlled_add_subtract_28_remainder_out),
    .carry_in(cas_controlled_add_subtract_35_carry_out));
  not not_8 (Q1, cas_controlled_add_subtract_28_remainder_out);
  CAS___controlled_add_subtract cas_controlled_add_subtract_29 (
    .carry_out(cas_controlled_add_subtract_29_carry_out), .T(not_1_out), .remainder_in(A7), .divisor(B0),
    .remainder_out(cas_controlled_add_subtract_29_remainder_out), .carry_in(not_1_out));
  CAS___controlled_add_subtract cas_controlled_add_subtract_30 (
    .carry_out(cas_controlled_add_subtract_30_carry_out), .T(Q7),
    .remainder_in(cas_controlled_add_subtract_29_remainder_out), .divisor(B1),
    .remainder_out(cas_controlled_add_subtract_30_remainder_out),
    .carry_in(cas_controlled_add_subtract_37_carry_out));
  CAS___controlled_add_subtract cas_controlled_add_subtract_31 (
    .carry_out(cas_controlled_add_subtract_31_carry_out), .T(Q6),
    .remainder_in(cas_controlled_add_subtract_30_remainder_out), .divisor(B2),
    .remainder_out(cas_controlled_add_subtract_31_remainder_out),
    .carry_in(cas_controlled_add_subtract_38_carry_out));
  CAS___controlled_add_subtract cas_controlled_add_subtract_32 (
    .carry_out(cas_controlled_add_subtract_32_carry_out), .T(Q5),
    .remainder_in(cas_controlled_add_subtract_31_remainder_out), .divisor(B3),
    .remainder_out(cas_controlled_add_subtract_32_remainder_out),
    .carry_in(cas_controlled_add_subtract_39_carry_out));
  CAS___controlled_add_subtract cas_controlled_add_subtract_33 (
    .carry_out(cas_controlled_add_subtract_33_carry_out), .T(Q4),
    .remainder_in(cas_controlled_add_subtract_32_remainder_out), .divisor(B4),
    .remainder_out(cas_controlled_add_subtract_33_remainder_out),
    .carry_in(cas_controlled_add_subtract_40_carry_out));
  CAS___controlled_add_subtract cas_controlled_add_subtract_34 (
    .carry_out(cas_controlled_add_subtract_34_carry_out), .T(Q3),
    .remainder_in(cas_controlled_add_subtract_33_remainder_out), .divisor(B5),
    .remainder_out(cas_controlled_add_subtract_34_remainder_out),
    .carry_in(cas_controlled_add_subtract_41_carry_out));
  CAS___controlled_add_subtract cas_controlled_add_subtract_35 (
    .carry_out(cas_controlled_add_subtract_35_carry_out), .T(Q2),
    .remainder_in(cas_controlled_add_subtract_34_remainder_out), .divisor(B6),
    .remainder_out(cas_controlled_add_subtract_35_remainder_out),
    .carry_in(cas_controlled_add_subtract_42_carry_out));
  CAS___controlled_add_subtract cas_controlled_add_subtract_36 (
    .carry_out(cas_controlled_add_subtract_36_carry_out), .T(Q1),
    .remainder_in(cas_controlled_add_subtract_35_remainder_out), .divisor(B7),
    .remainder_out(cas_controlled_add_subtract_36_remainder_out),
    .carry_in(cas_controlled_add_subtract_43_carry_out));
  not not_9 (Q0, cas_controlled_add_subtract_36_remainder_out);
  CAS___controlled_add_subtract cas_controlled_add_subtract_37 (
    .carry_out(cas_controlled_add_subtract_37_carry_out), .T(Q7), .remainder_in(A6), .divisor(B0),
    .remainder_out(cas_controlled_add_subtract_37_remainder_out), .carry_in(Q7));
  CAS___controlled_add_subtract cas_controlled_add_subtract_38 (
    .carry_out(cas_controlled_add_subtract_38_carry_out), .T(Q6),
    .remainder_in(cas_controlled_add_subtract_37_remainder_out), .divisor(B1),
    .remainder_out(cas_controlled_add_subtract_38_remainder_out),
    .carry_in(cas_controlled_add_subtract_44_carry_out));
  CAS___controlled_add_subtract cas_controlled_add_subtract_39 (
    .carry_out(cas_controlled_add_subtract_39_carry_out), .T(Q5),
    .remainder_in(cas_controlled_add_subtract_38_remainder_out), .divisor(B2),
    .remainder_out(cas_controlled_add_subtract_39_remainder_out),
    .carry_in(cas_controlled_add_subtract_45_carry_out));
  CAS___controlled_add_subtract cas_controlled_add_subtract_40 (
    .carry_out(cas_controlled_add_subtract_40_carry_out), .T(Q4),
    .remainder_in(cas_controlled_add_subtract_39_remainder_out), .divisor(B3),
    .remainder_out(cas_controlled_add_subtract_40_remainder_out),
    .carry_in(cas_controlled_add_subtract_46_carry_out));
  CAS___controlled_add_subtract cas_controlled_add_subtract_41 (
    .carry_out(cas_controlled_add_subtract_41_carry_out), .T(Q3),
    .remainder_in(cas_controlled_add_subtract_40_remainder_out), .divisor(B4),
    .remainder_out(cas_controlled_add_subtract_41_remainder_out),
    .carry_in(cas_controlled_add_subtract_47_carry_out));
  CAS___controlled_add_subtract cas_controlled_add_subtract_42 (
    .carry_out(cas_controlled_add_subtract_42_carry_out), .T(Q2),
    .remainder_in(cas_controlled_add_subtract_41_remainder_out), .divisor(B5),
    .remainder_out(cas_controlled_add_subtract_42_remainder_out),
    .carry_in(cas_controlled_add_subtract_48_carry_out));
  CAS___controlled_add_subtract cas_controlled_add_subtract_43 (
    .carry_out(cas_controlled_add_subtract_43_carry_out), .T(Q1),
    .remainder_in(cas_controlled_add_subtract_42_remainder_out), .divisor(B6),
    .remainder_out(cas_controlled_add_subtract_43_remainder_out),
    .carry_in(cas_controlled_add_subtract_49_carry_out));
  CAS___controlled_add_subtract cas_controlled_add_subtract_44 (
    .carry_out(cas_controlled_add_subtract_44_carry_out), .T(Q6), .remainder_in(A5), .divisor(B0),
    .remainder_out(cas_controlled_add_subtract_44_remainder_out), .carry_in(Q6));
  CAS___controlled_add_subtract cas_controlled_add_subtract_45 (
    .carry_out(cas_controlled_add_subtract_45_carry_out), .T(Q5),
    .remainder_in(cas_controlled_add_subtract_44_remainder_out), .divisor(B1),
    .remainder_out(cas_controlled_add_subtract_45_remainder_out),
    .carry_in(cas_controlled_add_subtract_50_carry_out));
  CAS___controlled_add_subtract cas_controlled_add_subtract_46 (
    .carry_out(cas_controlled_add_subtract_46_carry_out), .T(Q4),
    .remainder_in(cas_controlled_add_subtract_45_remainder_out), .divisor(B2),
    .remainder_out(cas_controlled_add_subtract_46_remainder_out),
    .carry_in(cas_controlled_add_subtract_51_carry_out));
  CAS___controlled_add_subtract cas_controlled_add_subtract_47 (
    .carry_out(cas_controlled_add_subtract_47_carry_out), .T(Q3),
    .remainder_in(cas_controlled_add_subtract_46_remainder_out), .divisor(B3),
    .remainder_out(cas_controlled_add_subtract_47_remainder_out),
    .carry_in(cas_controlled_add_subtract_52_carry_out));
  CAS___controlled_add_subtract cas_controlled_add_subtract_48 (
    .carry_out(cas_controlled_add_subtract_48_carry_out), .T(Q2),
    .remainder_in(cas_controlled_add_subtract_47_remainder_out), .divisor(B4),
    .remainder_out(cas_controlled_add_subtract_48_remainder_out),
    .carry_in(cas_controlled_add_subtract_53_carry_out));
  CAS___controlled_add_subtract cas_controlled_add_subtract_49 (
    .carry_out(cas_controlled_add_subtract_49_carry_out), .T(Q1),
    .remainder_in(cas_controlled_add_subtract_48_remainder_out), .divisor(B5),
    .remainder_out(cas_controlled_add_subtract_49_remainder_out),
    .carry_in(cas_controlled_add_subtract_54_carry_out));
  CAS___controlled_add_subtract cas_controlled_add_subtract_50 (
    .carry_out(cas_controlled_add_subtract_50_carry_out), .T(Q5), .remainder_in(A4), .divisor(B0),
    .remainder_out(cas_controlled_add_subtract_50_remainder_out), .carry_in(Q5));
  CAS___controlled_add_subtract cas_controlled_add_subtract_51 (
    .carry_out(cas_controlled_add_subtract_51_carry_out), .T(Q4),
    .remainder_in(cas_controlled_add_subtract_50_remainder_out), .divisor(B1),
    .remainder_out(cas_controlled_add_subtract_51_remainder_out),
    .carry_in(cas_controlled_add_subtract_55_carry_out));
  CAS___controlled_add_subtract cas_controlled_add_subtract_52 (
    .carry_out(cas_controlled_add_subtract_52_carry_out), .T(Q3),
    .remainder_in(cas_controlled_add_subtract_51_remainder_out), .divisor(B2),
    .remainder_out(cas_controlled_add_subtract_52_remainder_out),
    .carry_in(cas_controlled_add_subtract_56_carry_out));
  CAS___controlled_add_subtract cas_controlled_add_subtract_53 (
    .carry_out(cas_controlled_add_subtract_53_carry_out), .T(Q2),
    .remainder_in(cas_controlled_add_subtract_52_remainder_out), .divisor(B3),
    .remainder_out(cas_controlled_add_subtract_53_remainder_out),
    .carry_in(cas_controlled_add_subtract_57_carry_out));
  CAS___controlled_add_subtract cas_controlled_add_subtract_54 (
    .carry_out(cas_controlled_add_subtract_54_carry_out), .T(Q1),
    .remainder_in(cas_controlled_add_subtract_53_remainder_out), .divisor(B4),
    .remainder_out(cas_controlled_add_subtract_54_remainder_out),
    .carry_in(cas_controlled_add_subtract_58_carry_out));
  CAS___controlled_add_subtract cas_controlled_add_subtract_55 (
    .carry_out(cas_controlled_add_subtract_55_carry_out), .T(Q4), .remainder_in(A3), .divisor(B0),
    .remainder_out(cas_controlled_add_subtract_55_remainder_out), .carry_in(Q4));
  CAS___controlled_add_subtract cas_controlled_add_subtract_56 (
    .carry_out(cas_controlled_add_subtract_56_carry_out), .T(Q3),
    .remainder_in(cas_controlled_add_subtract_55_remainder_out), .divisor(B1),
    .remainder_out(cas_controlled_add_subtract_56_remainder_out),
    .carry_in(cas_controlled_add_subtract_59_carry_out));
  CAS___controlled_add_subtract cas_controlled_add_subtract_57 (
    .carry_out(cas_controlled_add_subtract_57_carry_out), .T(Q2),
    .remainder_in(cas_controlled_add_subtract_56_remainder_out), .divisor(B2),
    .remainder_out(cas_controlled_add_subtract_57_remainder_out),
    .carry_in(cas_controlled_add_subtract_60_carry_out));
  CAS___controlled_add_subtract cas_controlled_add_subtract_58 (
    .carry_out(cas_controlled_add_subtract_58_carry_out), .T(Q1),
    .remainder_in(cas_controlled_add_subtract_57_remainder_out), .divisor(B3),
    .remainder_out(cas_controlled_add_subtract_58_remainder_out),
    .carry_in(cas_controlled_add_subtract_61_carry_out));
  CAS___controlled_add_subtract cas_controlled_add_subtract_59 (
    .carry_out(cas_controlled_add_subtract_59_carry_out), .T(Q3), .remainder_in(A2), .divisor(B0),
    .remainder_out(cas_controlled_add_subtract_59_remainder_out), .carry_in(Q3));
  CAS___controlled_add_subtract cas_controlled_add_subtract_60 (
    .carry_out(cas_controlled_add_subtract_60_carry_out), .T(Q2),
    .remainder_in(cas_controlled_add_subtract_59_remainder_out), .divisor(B1),
    .remainder_out(cas_controlled_add_subtract_60_remainder_out),
    .carry_in(cas_controlled_add_subtract_62_carry_out));
  CAS___controlled_add_subtract cas_controlled_add_subtract_61 (
    .carry_out(cas_controlled_add_subtract_61_carry_out), .T(Q1),
    .remainder_in(cas_controlled_add_subtract_60_remainder_out), .divisor(B2),
    .remainder_out(cas_controlled_add_subtract_61_remainder_out),
    .carry_in(cas_controlled_add_subtract_63_carry_out));
  CAS___controlled_add_subtract cas_controlled_add_subtract_62 (
    .carry_out(cas_controlled_add_subtract_62_carry_out), .T(Q2), .remainder_in(A1), .divisor(B0),
    .remainder_out(cas_controlled_add_subtract_62_remainder_out), .carry_in(Q2));
  CAS___controlled_add_subtract cas_controlled_add_subtract_63 (
    .carry_out(cas_controlled_add_subtract_63_carry_out), .T(Q1),
    .remainder_in(cas_controlled_add_subtract_62_remainder_out), .divisor(B1),
    .remainder_out(cas_controlled_add_subtract_63_remainder_out),
    .carry_in(cas_controlled_add_subtract_64_carry_out));
  CAS___controlled_add_subtract cas_controlled_add_subtract_64 (
    .carry_out(cas_controlled_add_subtract_64_carry_out), .T(Q1), .remainder_in(A0), .divisor(B0),
    .remainder_out(cas_controlled_add_subtract_64_remainder_out), .carry_in(Q1));
endmodule

module Negative (
  input  A0,
  input  A1,
  input  A2,
  input  A3,
  input  A4,
  input  A5,
  input  A6,
  input  A7,
  input  B0,
  input  B1,
  input  B2,
  input  B3,
  input  B4,
  input  B5,
  input  B6,
  input  B7,
  output R7,
  output R6,
  output R5,
  output R4,
  output R3,
  output R2,
  output R1,
  output R0
);

  wire adder8bit_1_r0, adder8bit_1_r1, adder8bit_1_r2, adder8bit_1_r3, adder8bit_1_r4, adder8bit_1_r5,
       adder8bit_1_r6, adder8bit_1_r7, not_1_out, not_2_out, not_3_out, not_4_out, not_5_out, not_6_out,
       not_7_out, not_8_out;

  not not_1 (not_1_out, B0);
  not not_2 (not_2_out, B1);
  not not_3 (not_3_out, B2);
  not not_4 (not_4_out, B3);
  not not_5 (not_5_out, B4);
  not not_6 (not_6_out, B5);
  not not_7 (not_7_out, B6);
  not not_8 (not_8_out, B7);
  Adder8Bit adder8bit_1 (
    .A0(not_1_out), .A1(not_2_out), .A2(not_3_out), .A3(not_4_out), .A4(not_5_out), .A5(not_6_out),
    .A6(not_7_out), .A7(not_8_out), .B0(1'b1), .B1(1'b0), .B2(1'b0), .B3(1'b0), .B4(1'b0), .B5(1'b0),
    .B6(1'b0), .B7(1'b0), .R7(adder8bit_1_r7), .R6(adder8bit_1_r6), .R5(adder8bit_1_r5), .R4(adder8bit_1_r4),
    .R3(adder8bit_1_r3), .R2(adder8bit_1_r2), .R1(adder8bit_1_r1), .R0(adder8bit_1_r0), .CarryIn(1'b0));  // open: OVERFLOW
  Adder8Bit adder8bit_2 (
    .A0(A0), .A1(A1), .A2(A2), .A3(A3), .A4(A4), .A5(A5), .A6(A6), .A7(A7), .B0(adder8bit_1_r0),
    .B1(adder8bit_1_r1), .B2(adder8bit_1_r2), .B3(adder8bit_1_r3), .B4(adder8bit_1_r4), .B5(adder8bit_1_r5),
    .B6(adder8bit_1_r6), .B7(adder8bit_1_r7), .R7(R7), .R6(R6), .R5(R5), .R4(R4), .R3(R3), .R2(R2), .R1(R1),
    .R0(R0), .CarryIn(1'b0));  // open: OVERFLOW

  // Notes on the sheet:
  //   Número A
  //   Número B
  //   Usando método dos complementos
endmodule

module Kick_starter (
  output out_1
);

  wire clock_1_out, register_1_q;

  Clock clock_1 (.out(clock_1_out));
  Register #(.width(1), .trigger("high")) register_1 (.D(out_1), .Q(register_1_q), .clk(1'b1));  // open: en, clr
  or or_1 (out_1, clock_1_out, register_1_q);

  // Notes on the sheet:
  //   Kickstarter: vale 0 na primeira iteração e 1 em todas as outras
endmodule

module Retroactive (
  input  init,
  input  next,
  output out_3
);

  wire clock_1_out, kick_starter_1_out_1, register_1_q;

  Register #(.width(1)) register_1 (.D(next), .Q(register_1_q), .clk(clock_1_out));  // open: en, clr
  Clock clock_1 (.out(clock_1_out));
  Kick_starter kick_starter_1 (.out_1(kick_starter_1_out_1));
  Multiplexer #(.enable("false")) multiplexer_1 (
    .in0(init), .in1(register_1_q), .out(out_3), .sel(kick_starter_1_out_1));

  // Notes on the sheet:
  //   Recebe valor inicial e próximos valores
endmodule

module Inversor_de_sinal (
  input  B0,
  input  B1,
  input  B2,
  input  B3,
  input  B4,
  input  B5,
  input  B6,
  input  B7,
  output R7,
  output R6,
  output R5,
  output R4,
  output R3,
  output R2,
  output R1,
  output R0
);

  wire not_1_out, not_2_out, not_3_out, not_4_out, not_5_out, not_6_out, not_7_out, not_8_out;

  not not_1 (not_1_out, B0);
  not not_2 (not_2_out, B1);
  not not_3 (not_3_out, B2);
  not not_4 (not_4_out, B3);
  not not_5 (not_5_out, B4);
  not not_6 (not_6_out, B5);
  not not_7 (not_7_out, B6);
  not not_8 (not_8_out, B7);
  Adder8Bit adder8bit_1 (
    .A0(not_1_out), .A1(not_2_out), .A2(not_3_out), .A3(not_4_out), .A4(not_5_out), .A5(not_6_out),
    .A6(not_7_out), .A7(not_8_out), .B0(1'b1), .B1(1'b0), .B2(1'b0), .B3(1'b0), .B4(1'b0), .B5(1'b0),
    .B6(1'b0), .B7(1'b0), .R7(R7), .R6(R6), .R5(R5), .R4(R4), .R3(R3), .R2(R2), .R1(R1), .R0(R0),
    .CarryIn(1'b0));  // open: OVERFLOW
endmodule

module \Módulo  (
  input  B0,
  input  B1,
  input  B2,
  input  B3,
  input  B4,
  input  B5,
  input  B6,
  input  B7,
  output R0,
  output R1,
  output R2,
  output R3,
  output R4,
  output R5,
  output R6,
  output R7
);

  wire inversor_de_sinal_1_p2, inversor_de_sinal_1_p4, inversor_de_sinal_1_p6, inversor_de_sinal_1_p8,
       inversor_de_sinal_1_p10, inversor_de_sinal_1_p12, inversor_de_sinal_1_p14, inversor_de_sinal_1_p16;

  // Inversor_de_sinal inversor_de_sinal_1: pin names not known; wires that end beside it: B7, inversor_de_sinal_1_p2, B6, inversor_de_sinal_1_p4, B5, inversor_de_sinal_1_p6, B4, inversor_de_sinal_1_p8, B3, inversor_de_sinal_1_p10, B2, inversor_de_sinal_1_p12, B1, inversor_de_sinal_1_p14, B0, inversor_de_sinal_1_p16
  Multiplexer #(.enable("false")) multiplexer_1 (.in0(B0), .in1(inversor_de_sinal_1_p16), .out(R0), .sel(B7));
  Multiplexer #(.enable("false")) multiplexer_2 (.in0(B1), .in1(inversor_de_sinal_1_p14), .out(R1), .sel(B7));
  Multiplexer #(.enable("false")) multiplexer_3 (.in0(B2), .in1(inversor_de_sinal_1_p12), .out(R2), .sel(B7));
  Multiplexer #(.enable("false")) multiplexer_4 (.in0(B3), .in1(inversor_de_sinal_1_p10), .out(R3), .sel(B7));
  Multiplexer #(.enable("false")) multiplexer_5 (.in0(B4), .in1(inversor_de_sinal_1_p8), .out(R4), .sel(B7));
  Multiplexer #(.enable("false")) multiplexer_6 (.in0(B5), .in1(inversor_de_sinal_1_p6), .out(R5), .sel(B7));
  Multiplexer #(.enable("false")) multiplexer_7 (.in0(B6), .in1(inversor_de_sinal_1_p4), .out(R6), .sel(B7));
  Multiplexer #(.enable("false")) multiplexer_8 (.in0(B7), .in1(inversor_de_sinal_1_p2), .out(R7), .sel(B7));
endmodule

module \Divisão  (
  input  a0,
  input  a1,
  input  a2,
  input  a3,
  input  a4,
  input  a5,
  input  a6,
  input  a7,
  input  b0,
  input  b1,
  input  b2,
  input  b3,
  input  b4,
  input  b5,
  input  b6,
  input  b7,
  output r7,
  output r6,
  output r5,
  output r4,
  output r3,
  output r2,
  output r1,
  output r0
);

  wire and_1_out, clock_1_out, counter_5_q, inversor_de_sinal_1_p1, inversor_de_sinal_1_p2,
       inversor_de_sinal_1_p3, inversor_de_sinal_1_p4, inversor_de_sinal_1_p5, inversor_de_sinal_1_p6,
       inversor_de_sinal_1_p7, inversor_de_sinal_1_p8, inversor_de_sinal_1_p9, inversor_de_sinal_1_p10,
       inversor_de_sinal_1_p11, inversor_de_sinal_1_p12, inversor_de_sinal_1_p13, inversor_de_sinal_1_p14,
       inversor_de_sinal_1_p15, inversor_de_sinal_1_p16, multiplexer_1_out, multiplexer_2_out,
       multiplexer_3_out, multiplexer_4_out, multiplexer_5_out, multiplexer_6_out, multiplexer_7_out,
       multiplexer_8_out, \módulo_1_r0 , \módulo_1_r1 , \módulo_1_r2 , \módulo_1_r3 , \módulo_1_r4 ,
       \módulo_1_r5 , \módulo_1_r6 , \módulo_1_r7 , \módulo_2_r0 , \módulo_2_r1 , \módulo_2_r2 ,
       \módulo_2_r3 , \módulo_2_r4 , \módulo_2_r5 , \módulo_2_r6 , \módulo_2_r7 , negative_1_r0,
       negative_1_r1, negative_1_r2, negative_1_r3, negative_1_r4, negative_1_r5, negative_1_r6,
       negative_1_r7, not_1_out, retroactive_1_out_3, retroactive_2_out_3, retroactive_3_out_3,
       retroactive_4_out_3, retroactive_5_out_3, retroactive_6_out_3, retroactive_7_out_3,
       retroactive_8_out_3, xor_1_out;

  xor xor_1 (xor_1_out, a7, b7);
  // Inversor_de_sinal inversor_de_sinal_1: pin names not known; wires that end beside it: inversor_de_sinal_1_p1, inversor_de_sinal_1_p2, inversor_de_sinal_1_p3, inversor_de_sinal_1_p4, inversor_de_sinal_1_p5, inversor_de_sinal_1_p6, inversor_de_sinal_1_p7, inversor_de_sinal_1_p8, inversor_de_sinal_1_p9, inversor_de_sinal_1_p10, inversor_de_sinal_1_p11, inversor_de_sinal_1_p12, inversor_de_sinal_1_p13, inversor_de_sinal_1_p14, inversor_de_sinal_1_p15, inversor_de_sinal_1_p16
  \Módulo  \módulo_1  (
    .B0(a0), .B1(a1), .B2(a2), .B3(a3), .B4(a4), .B5(a5), .B6(a6), .B7(a7), .R0(\módulo_1_r0 ),
    .R1(\módulo_1_r1 ), .R2(\módulo_1_r2 ), .R3(\módulo_1_r3 ), .R4(\módulo_1_r4 ), .R5(\módulo_1_r5 ),
    .R6(\módulo_1_r6 ), .R7(\módulo_1_r7 ));
  Multiplexer #(.enable("false")) multiplexer_1 (
    .in0(inversor_de_sinal_1_p1), .in1(inversor_de_sinal_1_p2), .out(multiplexer_1_out), .sel(xor_1_out));
  D_Flip_Flop #(.trigger("high")) d_ff_1 (
    .clk(negative_1_r7), .D(multiplexer_1_out), .Q(r7));  // open: Qn, preset, en, reset
  D_Flip_Flop #(.trigger("high")) d_ff_2 (
    .clk(negative_1_r7), .D(multiplexer_2_out), .Q(r6));  // open: Qn, preset, en, reset
  Multiplexer #(.enable("false")) multiplexer_2 (
    .in0(inversor_de_sinal_1_p3), .in1(inversor_de_sinal_1_p4), .out(multiplexer_2_out), .sel(xor_1_out));
  Retroactive retroactive_1 (.init(\módulo_1_r0 ), .next(negative_1_r0), .out_3(retroactive_1_out_3));
  Retroactive retroactive_2 (.init(\módulo_1_r1 ), .next(negative_1_r1), .out_3(retroactive_2_out_3));
  Retroactive retroactive_3 (.init(\módulo_1_r2 ), .next(negative_1_r2), .out_3(retroactive_3_out_3));
  Retroactive retroactive_4 (.init(\módulo_1_r3 ), .next(negative_1_r3), .out_3(retroactive_4_out_3));
  Retroactive retroactive_5 (.init(\módulo_1_r4 ), .next(negative_1_r4), .out_3(retroactive_5_out_3));
  Retroactive retroactive_6 (.init(\módulo_1_r5 ), .next(negative_1_r5), .out_3(retroactive_6_out_3));
  Retroactive retroactive_7 (.init(\módulo_1_r6 ), .next(negative_1_r6), .out_3(retroactive_7_out_3));
  Retroactive retroactive_8 (.init(\módulo_1_r7 ), .next(negative_1_r7), .out_3(retroactive_8_out_3));
  \Módulo  \módulo_2  (
    .B0(b0), .B1(b1), .B2(b2), .B3(b3), .B4(b4), .B5(b5), .B6(b6), .B7(b7), .R0(\módulo_2_r0 ),
    .R1(\módulo_2_r1 ), .R2(\módulo_2_r2 ), .R3(\módulo_2_r3 ), .R4(\módulo_2_r4 ), .R5(\módulo_2_r5 ),
    .R6(\módulo_2_r6 ), .R7(\módulo_2_r7 ));
  Counter #(.width(1), .max('h1), .trigger("falling")) counter_1 (
    .Q(inversor_de_sinal_1_p1), .clk(inversor_de_sinal_1_p3));  // open: load, D, count, carry, clr
  Multiplexer #(.enable("false")) multiplexer_3 (
    .in0(inversor_de_sinal_1_p5), .in1(inversor_de_sinal_1_p6), .out(multiplexer_3_out), .sel(xor_1_out));
  Counter #(.width(1), .max('h1), .trigger("falling")) counter_2 (
    .Q(inversor_de_sinal_1_p3), .clk(inversor_de_sinal_1_p5));  // open: load, D, count, carry, clr
  D_Flip_Flop #(.trigger("high")) d_ff_3 (
    .clk(negative_1_r7), .D(multiplexer_3_out), .Q(r5));  // open: Qn, preset, en, reset
  Counter #(.width(1), .max('h1), .trigger("falling")) counter_3 (
    .Q(inversor_de_sinal_1_p5), .clk(inversor_de_sinal_1_p7));  // open: load, D, count, carry, clr
  Counter #(.width(1), .max('h1), .trigger("falling")) counter_4 (
    .Q(inversor_de_sinal_1_p7), .clk(inversor_de_sinal_1_p9));  // open: load, D, count, carry, clr
  Multiplexer #(.enable("false")) multiplexer_4 (
    .in0(inversor_de_sinal_1_p7), .in1(inversor_de_sinal_1_p8), .out(multiplexer_4_out), .sel(xor_1_out));
  Negative negative_1 (
    .A0(retroactive_1_out_3), .A1(retroactive_2_out_3), .A2(retroactive_3_out_3), .A3(retroactive_4_out_3),
    .A4(retroactive_5_out_3), .A5(retroactive_6_out_3), .A6(retroactive_7_out_3), .A7(retroactive_8_out_3),
    .B0(\módulo_2_r0 ), .B1(\módulo_2_r1 ), .B2(\módulo_2_r2 ), .B3(\módulo_2_r3 ), .B4(\módulo_2_r4 ),
    .B5(\módulo_2_r5 ), .B6(\módulo_2_r6 ), .B7(\módulo_2_r7 ), .R7(negative_1_r7), .R6(negative_1_r6),
    .R5(negative_1_r5), .R4(negative_1_r4), .R3(negative_1_r3), .R2(negative_1_r2), .R1(negative_1_r1),
    .R0(negative_1_r0));
  Clock clock_1 (.out(clock_1_out));
  not not_1 (not_1_out, negative_1_r7);
  Counter #(.width(1), .max('h1)) counter_5 (.Q(counter_5_q), .clk(clock_1_out));  // open: load, D, count, carry, clr
  and and_1 (and_1_out, not_1_out, counter_5_q);
  Counter #(.width(1), .max('h1), .trigger("falling")) counter_6 (
    .Q(inversor_de_sinal_1_p9), .clk(inversor_de_sinal_1_p11));  // open: load, D, count, carry, clr
  D_Flip_Flop #(.trigger("high")) d_ff_4 (
    .clk(negative_1_r7), .D(multiplexer_4_out), .Q(r4));  // open: Qn, preset, en, reset
  Counter #(.width(1), .max('h1), .trigger("falling")) counter_7 (
    .Q(inversor_de_sinal_1_p11), .clk(inversor_de_sinal_1_p13));  // open: load, D, count, carry, clr
  Multiplexer #(.enable("false")) multiplexer_5 (
    .in0(inversor_de_sinal_1_p9), .in1(inversor_de_sinal_1_p10), .out(multiplexer_5_out), .sel(xor_1_out));
  Counter #(.width(1), .max('h1), .trigger("falling")) counter_8 (
    .Q(inversor_de_sinal_1_p13), .clk(inversor_de_sinal_1_p15));  // open: load, D, count, carry, clr
  D_Flip_Flop #(.trigger("high")) d_ff_5 (
    .clk(negative_1_r7), .D(multiplexer_5_out), .Q(r3));  // open: Qn, preset, en, reset
  Counter #(.width(1), .max('h1), .trigger("falling")) counter_9 (
    .Q(inversor_de_sinal_1_p15), .clk(and_1_out));  // open: load, D, count, carry, clr
  D_Flip_Flop #(.trigger("high")) d_ff_6 (
    .clk(negative_1_r7), .D(multiplexer_6_out), .Q(r2));  // open: Qn, preset, en, reset
  Multiplexer #(.enable("false")) multiplexer_6 (
    .in0(inversor_de_sinal_1_p11), .in1(inversor_de_sinal_1_p12), .out(multiplexer_6_out), .sel(xor_1_out));
  Multiplexer #(.enable("false")) multiplexer_7 (
    .in0(inversor_de_sinal_1_p13), .in1(inversor_de_sinal_1_p14), .out(multiplexer_7_out), .sel(xor_1_out));
  D_Flip_Flop #(.trigger("high")) d_ff_7 (
    .clk(negative_1_r7), .D(multiplexer_7_out), .Q(r1));  // open: Qn, preset, en, reset
  Multiplexer #(.enable("false")) multiplexer_8 (
    .in0(inversor_de_sinal_1_p15), .in1(inversor_de_sinal_1_p16), .out(multiplexer_8_out), .sel(xor_1_out));
  D_Flip_Flop #(.trigger("high")) d_ff_8 (
    .clk(negative_1_r7), .D(multiplexer_8_out), .Q(r0));  // open: Qn, preset, en, reset

  // Notes on the sheet:
  //   Diminui o módulo de um do outro até ficar negativo
  //   Por um erro do logisin (no final 0 AND 1 fica 1)
  //   As vezes temos off-by-one (tentar 100 / 001)
endmodule

module \main_Divisão  (
  input  A7,
  input  A6,
  input  A5,
  input  A4,
  input  A3,
  input  A2,
  input  A1,
  input  A0,
  input  B7,
  input  B6,
  input  B5,
  input  B4,
  input  B3,
  input  B2,
  input  B1,
  input  B0,
  output R7,
  output R6,
  output R5,
  output R4,
  output R3,
  output R2,
  output R1,
  output R0
);

  \Divisão  \divisão_1  (
    .a0(A0), .a1(A1), .a2(A2), .a3(A3), .a4(A4), .a5(A5), .a6(A6), .a7(A7), .b0(B0), .b1(B1), .b2(B2),
    .b3(B3), .b4(B4), .b5(B5), .b6(B6), .b7(B7), .r7(R7), .r6(R6), .r5(R5), .r4(R4), .r3(R3), .r2(R2),
    .r1(R1), .r0(R0));

  // Other names for the same wires on the sheet: divOVERFLOW = R7

  // Notes on the sheet:
  //   DIVISAO
  //   DIVISAO
endmodule
