// Logisim project IF.circ as structural Verilog: 1 circuit, main circuit main
module main (
  input  in_1,
  input  [7:0] in_2,
  output ADD,
  output SUB,
  output out_5,
  output out_6,
  output REM,
  output NOP,
  output Load,
  output STA,
  output JMP,
  output STP,
  output INN,
  output PRN,
  output JLE,
  output JDZ,
  output JGT,
  output JEQ,
  output JLT,
  output out_20
);

  wire and_4_out, and_5_out, and_6_out, and_10_out, and_11_out, and_12_out, and_16_out, and_17_out,
       and_18_out, and_22_out, and_23_out, and_24_out, and_28_out, and_29_out, and_30_out, and_33_out,
       and_35_out, and_36_out;

  and and_1 (ADD, in_1, and_4_out);
  and and_2 (INN, in_1, and_5_out);
  and and_3 (JLE, in_1, and_6_out);
  and and_4 (and_4_out, in_2[0], ~in_2[1], in_2[2], ~in_2[3], in_2[4], ~in_2[5], ~in_2[6], ~in_2[7]);  // AND_Gate
  and and_5 (and_5_out, in_2[0], in_2[1], in_2[2], in_2[3], in_2[4], ~in_2[5], ~in_2[6], ~in_2[7]);  // AND_Gate
  and and_6 (and_6_out, ~in_2[0], ~in_2[1], in_2[2], ~in_2[3], in_2[4], in_2[5], ~in_2[6], ~in_2[7]);  // AND_Gate
  and and_7 (SUB, in_1, and_10_out);
  and and_8 (PRN, in_1, and_11_out);
  and and_9 (JDZ, in_1, and_12_out);
  and and_10 (and_10_out, ~in_2[0], in_2[1], in_2[2], ~in_2[3], in_2[4], ~in_2[5], ~in_2[6], ~in_2[7]);  // AND_Gate
  and and_11 (and_11_out, in_2[0], ~in_2[1], ~in_2[2], in_2[3], ~in_2[4], in_2[5], ~in_2[6], ~in_2[7]);  // AND_Gate
  and and_12 (and_12_out, in_2[0], ~in_2[1], in_2[2], ~in_2[3], in_2[4], in_2[5], ~in_2[6], ~in_2[7]);  // AND_Gate
  and and_13 (out_5, in_1, and_16_out);
  and and_14 (Load, in_1, and_17_out);
  and and_15 (JGT, in_1, and_18_out);
  and and_16 (and_16_out, in_2[0], in_2[1], in_2[2], ~in_2[3], in_2[4], ~in_2[5], ~in_2[6], ~in_2[7]);  // AND_Gate
  and and_17 (and_17_out, in_2[0], in_2[1], ~in_2[2], in_2[3], ~in_2[4], ~in_2[5], ~in_2[6], ~in_2[7]);  // AND_Gate
  and and_18 (and_18_out, ~in_2[0], in_2[1], in_2[2], ~in_2[3], in_2[4], in_2[5], ~in_2[6], ~in_2[7]);  // AND_Gate
  and and_19 (out_6, in_1, and_23_out);
  and and_20 (STA, in_1, and_22_out);
  and and_21 (JEQ, in_1, and_24_out);
  and and_22 (and_22_out, ~in_2[0], ~in_2[1], in_2[2], in_2[3], ~in_2[4], ~in_2[5], ~in_2[6], ~in_2[7]);  // AND_Gate
  and and_23 (and_23_out, ~in_2[0], ~in_2[1], ~in_2[2], in_2[3], in_2[4], ~in_2[5], ~in_2[6], ~in_2[7]);  // AND_Gate
  and and_24 (and_24_out, in_2[0], in_2[1], in_2[2], ~in_2[3], in_2[4], in_2[5], ~in_2[6], ~in_2[7]);  // AND_Gate
  and and_25 (REM, in_1, and_29_out);
  and and_26 (JMP, in_1, and_28_out);
  and and_27 (JLT, in_1, and_30_out);
  and and_28 (and_28_out, in_2[0], in_2[1], ~in_2[2], ~in_2[3], in_2[4], in_2[5], ~in_2[6], ~in_2[7]);  // AND_Gate
  and and_29 (and_29_out, in_2[0], ~in_2[1], ~in_2[2], in_2[3], in_2[4], ~in_2[5], ~in_2[6], ~in_2[7]);  // AND_Gate
  and and_30 (and_30_out, ~in_2[0], ~in_2[1], ~in_2[2], in_2[3], in_2[4], in_2[5], ~in_2[6], ~in_2[7]);  // AND_Gate
  and and_31 (STP, in_1, and_33_out);
  and and_32 (NOP, in_1, and_35_out);
  and and_33 (and_33_out, ~in_2[0], in_2[1], in_2[2], ~in_2[3], ~in_2[4], ~in_2[5], in_2[6], ~in_2[7]);  // AND_Gate
  and and_34 (out_20, in_1, and_36_out);
  and and_35 (and_35_out, ~in_2[0], in_2[1], ~in_2[2], ~in_2[3], in_2[4], in_2[5], ~in_2[6], ~in_2[7]);  // AND_Gate
  and and_36 (and_36_out, in_2[0], ~in_2[1], ~in_2[2], in_2[3], in_2[4], in_2[5], ~in_2[6], ~in_2[7]);  // AND_Gate

  // Other names for the same wires on the sheet: Enable = in_1; _0 = in_2[0]; _1 = in_2[1]; _2 = in_2[2];
  //   _3 = in_2[3]; _4 = in_2[4]; _5 = in_2[5]; _6 = in_2[6]; _7 = in_2[7]

  // Notes on the sheet:
  //   MUL
  //   DIV
  //   JGE
endmodule
