// Logisim project Ula16bits.circ as structural Verilog: 1 circuit, main circuit main
module main (
  input  in_1,
  input  [15:0] in_2,
  input  [15:0] in_3,
  input  [2:0] in_4,
  output out_5,
  output [15:0] out_6
);

  wire nor_1_out, or_1_out, tunnel, tunnel_t;
  wire [15:0] _00A, _00B, _01A, _01B, _10A, _10B, _11A, _11B, _100A, _100B, A, adder_1_out, B, divider_1_out,
       divider_2_rem, multiplier_1_out, subtractor_1_out, x;

  assign A = in_2 & {16{in_1}};  // AND_Gate and_1, 16 bits wide
  Adder #(.width(16)) adder_1 (.a(_00A), .b(_00B), .out(adder_1_out), .cout(tunnel));  // open: cin
  Subtractor #(.width(16)) subtractor_1 (.a(_01A), .b(_01B), .out(subtractor_1_out), .bout(tunnel_t));  // open: bin
  Multiplier #(.width(16)) multiplier_1 (.a(_10A), .b(_10B), .out(multiplier_1_out), .cout(x));  // open: cin
  Divider #(.width(16)) divider_1 (.a(_11A), .b(_11B), .out(divider_1_out));  // open: upper, rem
  Divider #(.width(16)) divider_2 (.a(_100A), .b(_100B), .rem(divider_2_rem));  // open: out, upper
  Multiplexer #(.select(3), .width(16), .enable("false")) multiplexer_1 (
    .in0(adder_1_out), .in1(subtractor_1_out), .in2(multiplier_1_out), .in3(divider_1_out),
    .in4(divider_2_rem), .out(out_6), .sel(in_4));  // open: in5, in6, in7
  assign B = in_3 & {16{in_1}};  // AND_Gate and_2, 16 bits wide
  Demultiplexer #(.select(3), .width(16), .enable("false")) demultiplexer_1 (
    .out0(_00A), .out1(_01A), .out2(_10A), .out3(_11A), .out4(_100A), .in(A), .sel(in_4));  // open: out5, out6, out7
  nor nor_1 (nor_1_out, B[0], B[1], B[2], B[3], B[4], B[5], B[6], B[7], B[9], B[10], B[11], B[12], B[13], B[14], B[15], B[8]);
  Demultiplexer #(.select(3), .width(16), .enable("false")) demultiplexer_2 (
    .out0(_00B), .out1(_01B), .out2(_10B), .out3(_11B), .out4(_100B), .in(B), .sel(in_4));  // open: out5, out6, out7
  or or_1 (or_1_out, tunnel, tunnel_t, x[0], x[1], x[2], x[3], x[4], x[5], x[6], nor_1_out, x[7], x[8], x[9], x[10], x[11], x[12], x[13], x[14], x[15]);
  and and_3 (out_5, or_1_out, in_1);

  // Other names for the same wires on the sheet: ENABLE = in_1; ENABLE16[15:0] = {16{in_1}}; selecionador[2:0] = in_4

  // Notes on the sheet:
  //   modulos aritmeticos do Logisim
  //   entrada A e B
  //   selecionador da operacao
endmodule
