// Logisim project controlador.circ as structural Verilog: 1 circuit, main circuit main
module main (
  input  CLOCK,
  input  RESET,
  input  [7:0] PC,
  input  [15:0] ACC_OUT,
  input  [15:0] IR_OUT,
  input  [15:0] RAM_OUT,
  input  [15:0] INN,
  output [7:0] PC_SET,
  output PC_plus_plus,
  output [15:0] ACC_IN,
  output [15:0] IR_IN,
  output [15:0] RAM_IN,
  output [7:0] RAM_ADDR,
  output [15:0] OUT,
  output out_15,
  output RAM_CLOCK,
  output READ_ENABLE,
  output PC_ENABLE,
  output ACC_ENABLE,
  output IR_ENABLE
);

  wire and_1_out, CONTA, INN_t, JDZ, JEQ, JGE, JGT, JLE, JLT, JMP, LDA, main_4_p3, main_4_p4, main_4_p5,
       main_4_p6, main_4_p7, not_3_out, or_1_out, or_3_out, PRN, RAM_CLOCK_t, STA, STOP;
  wire [1:0] counter_1_q;
  wire [2:0] main_2_out_3;
  wire [15:0] ACC_CONTA, ACC_RAM, OUT_MEM;

  Demultiplexer #(.select(2), .width(16), .enable("false")) demultiplexer_1 (
    .out0(IR_IN), .out1(ACC_RAM), .out2(OUT_MEM), .in(RAM_OUT), .sel({PRN, LDA}));  // open: out3
  Multiplexer #(.width(16), .enable("false")) multiplexer_1 (.in0(INN), .in1(ACC_OUT), .out(RAM_IN), .sel(STA));
  not not_1 (RAM_CLOCK, RAM_CLOCK_t);
  // Jumpador_main main_1: pin names not known; wires that end beside it: JMP, JLE, JDZ, JGT, JEQ, JLT, JGE, ACC_OUT, PC_ENABLE
  Counter #(.width(2), .max('h2)) counter_1 (
    .Q(counter_1_q), .clk(and_1_out), .clr(RESET));  // open: load, D, count, carry
  and and_1 (and_1_out, CLOCK, ~STOP);  // AND_Gate
  or or_1 (or_1_out, STA, INN_t);
  not not_2 (READ_ENABLE, or_1_out);
  not not_3 (not_3_out, RAM_CLOCK_t);
  Demultiplexer #(.select(2), .enable("false")) demultiplexer_2 (
    .out0(IR_ENABLE), .out1(RAM_CLOCK_t), .out2(PC_plus_plus), .in(1'b1), .sel(counter_1_q));  // open: out3
  Register #(.width(16)) register_1 (.D(OUT_MEM), .en(PRN), .Q(OUT), .clk(not_3_out));  // open: clr
  or or_2 (ACC_ENABLE, LDA, CONTA);
  or or_3 (or_3_out, INN_t, LDA, CONTA, PRN, STA);
  tradutor_main main_2 (.in_2(IR_OUT[15:8]), .out_3(main_2_out_3), .in_1(CONTA));
  Multiplexer #(.width(8), .enable("false")) multiplexer_2 (
    .in0(PC), .in1(IR_OUT[7:0]), .out(RAM_ADDR), .sel(or_3_out));
  Ula16bits_main main_3 (
    .out_6(ACC_CONTA), .out_5(out_15), .in_4(main_2_out_3), .in_2(ACC_OUT), .in_3(IR_IN), .in_1(CONTA));
  // IFao_main main_4: pin names not known; wires that end beside it: IR_OUT[15:8], RAM_CLOCK_t, main_4_p3, main_4_p4, main_4_p5, main_4_p6, main_4_p7, JLE, JDZ, JGT, JEQ, JLT, JGE, INN_t, PRN, LDA, STA
  Multiplexer #(.width(16), .enable("false")) multiplexer_3 (.in0(ACC_RAM), .in1(ACC_CONTA), .out(ACC_IN), .sel(CONTA));
  or or_4 (CONTA, main_4_p3, main_4_p4, main_4_p5, main_4_p6, main_4_p7);

  assign PC_SET = IR_OUT[7:0];

  // Other names for the same wires on the sheet: IN[15:0] = INN; IR_ADDR[7:0] = IR_OUT[7:0];
  //   IR_INST[7:0] = IR_OUT[15:8]; OVERFLOW = out_15; PEGA_PC = IR_ENABLE

  // Notes on the sheet:
  //   Circuito para os JUMP
  //   Tratamento da entrada e saida
  //   Selecionador da operacao
  //   ULA16
  //   quando CONTA estiver ativada, carregamos o dado armazenado no Acumulador
  //   Conjunto de instruções
endmodule
