// Logisim project ep3.circ as structural Verilog: 1 circuit, main circuit main
module main (
  input  [15:0] ENTRADA,
  output [15:0] SAIDA
);

  wire ACC_EN, button_2_out, CLOCK, IR_EN, not_1_out, OVERF, PC_EN, PC_plus_plus, RAM_CK, RAM_READ, RESET;
  wire [7:0] PC, PC_SET, RAM_ADDR;
  wire [15:0] ACC_I, ACC_O, IR_I, IR_O, ram_1_data, RAM_I, RAM_O;

  Register #(.width(16)) ACC (.D(ACC_I), .en(ACC_EN), .Q(ACC_O), .clk(CLOCK), .clr(RESET));
  Register #(.width(16)) register_1 (.D(IR_I), .en(IR_EN), .Q(IR_O), .clk(CLOCK), .clr(RESET));
  controlador_main main_1 (
    .PC(PC), .ACC_OUT(ACC_O), .IR_OUT(IR_O), .RAM_OUT(RAM_O), .PC_plus_plus(PC_plus_plus), .ACC_IN(ACC_I),
    .IR_IN(IR_I), .RAM_ADDR(RAM_ADDR), .CLOCK(CLOCK), .RESET(RESET), .RAM_CLOCK(RAM_CK),
    .READ_ENABLE(RAM_READ), .PC_ENABLE(PC_EN), .ACC_ENABLE(ACC_EN), .IR_ENABLE(IR_EN), .PC_SET(PC_SET),
    .INN(ENTRADA), .OUT(SAIDA), .RAM_IN(RAM_I), .out_15(OVERF));
  Button button_1 (.out(RESET));
  Clock clock_1 (.out(CLOCK));
  PC_main main_2 (.count_up(PC_plus_plus), .reset(RESET), .out_5(PC), .in_4(PC_SET), .load(PC_EN));
  RAM #(.dataWidth(16)) ram_1 (
    .addr(RAM_ADDR), .data(ram_1_data), .sel(1'b1), .clk(RAM_CK), .ld(RAM_READ), .clr(button_2_out));
  Button button_2 (.out(button_2_out));
  not not_1 (not_1_out, RAM_READ);
  Transistor #(.\type ("n"), .width(16)) transistor_1 (.in(RAM_I), .out(ram_1_data), .gate(not_1_out));
  Transistor #(.\type ("n"), .width(16)) transistor_2 (.in(ram_1_data), .out(RAM_O), .gate(RAM_READ));

  // Notes on the sheet:
  //   Insira na ENTRADA um numero em binario
  //   CONTROLADOR:
  //   Inclua a lista de instruções do arquivo "StoH" ou "Factorial". Utilize os dois botões abaixo para iniciar o teste.
  //   Resultado será impresso em SAIDA
  //   RAM
endmodule
