// Logisim project tradutor.circ as structural Verilog: 1 circuit, main circuit main
module main (
  input  in_1,
  input  [7:0] in_2,
  output [2:0] out_3
);

  wire and_2_out, and_3_out, not_1_out, not_2_out, not_3_out, X, Y, Z;

  not not_1 (not_1_out, in_2[2]);
  not not_2 (not_2_out, in_2[2]);
  and and_1 (X, in_2[0], not_1_out);
  not not_3 (not_3_out, in_2[0]);
  and and_2 (and_2_out, in_2[1], in_2[0]);
  and and_3 (and_3_out, not_2_out, not_3_out);
  or or_1 (Y, and_3_out, and_2_out);
  not not_4 (Z, in_2[0]);
  and and_4 (out_3[0], Z, in_1);
  and and_5 (out_3[1], Y, in_1);
  and and_6 (out_3[2], X, in_1);

  // Other names for the same wires on the sheet: ENABLE = in_1; C = in_2[0]; B = in_2[1]; A = in_2[2]

  // Notes on the sheet:
  //   Em decimal, as instruções 21 a 25 indicam a operação aritmética.
  //   Aqui ocorre a identificação da operação da instrução lida.
endmodule
